// Logisim project CPU ov.circ as structural Verilog: 56 circuits, main circuit main
module main (
  input  E,
  input  S,
  output [7:0] mc,
  output \buf 
);

  wire RESET_out;

  Keyboard keyboard_1 (.clk(E), .re(S), .clr(RESET_out), .avail(\buf ), .data(mc[6:0]));
  Button RESET (.out(RESET_out));
  // Pins of 7 and 8 bits meet at mc

  // Other names for the same wires on the sheet: IN1[7:0] = mc

  // Notes on the sheet:
  //   KEYBOARD
endmodule

module USER_PANEL_51aa35a4 (
  input  W,
  input  [23:0] RGB
);

  wire and_1_out, CLKE, CLKIN, CLKL, CLKS, CLR_out, DIS_CLK, EN, END, KB, KYB_CLK, r, TS;
  wire [4:0] FLAGS;
  wire [7:0] IN1, OUT1, X1, Y1;
  wire [15:0] FPU, IAR, IN2, IN3, INDEX, IR, OUT2, OUT3, R0, R1, R2, R3, R4, R5, R6_TEMP, SP;

  TTY #(.rows(16), .trigger("falling")) tty_1 (.data(OUT1[6:0]), .clk(CLKS), .we(DIS_CLK), .clr(r));
  Keyboard keyboard_1 (.clk(CLKS), .re(KYB_CLK), .clr(r), .avail(KB), .data(IN1[6:0]));
  Hex_Digit_Display hex_digit_display_1 (.value(R0[15:12]));  // open: dp
  Hex_Digit_Display hex_digit_display_2 (.value(SP[15:12]));  // open: dp
  Hex_Digit_Display hex_digit_display_3 (.value(R0[11:8]));  // open: dp
  Hex_Digit_Display hex_digit_display_4 (.value(R0[7:4]));  // open: dp
  Hex_Digit_Display hex_digit_display_5 (.value(SP[11:8]));  // open: dp
  Hex_Digit_Display hex_digit_display_6 (.value(SP[7:4]));  // open: dp
  Hex_Digit_Display hex_digit_display_7 (.value(R0[3:0]));  // open: dp
  Hex_Digit_Display hex_digit_display_8 (.value(SP[3:0]));  // open: dp
  Hex_Digit_Display hex_digit_display_9 (.value(R1[15:12]));  // open: dp
  Hex_Digit_Display hex_digit_display_10 (.value(R1[11:8]));  // open: dp
  Hex_Digit_Display hex_digit_display_11 (.value(INDEX[15:12]));  // open: dp
  Hex_Digit_Display hex_digit_display_12 (.value(INDEX[11:8]));  // open: dp
  // RGB_Video #(.height(256), .width(256)) rgb_video_1: pin names not known; wires that end beside it: r, CLKIN, 1'b1, X1, Y1, OUT2
  Hex_Digit_Display hex_digit_display_13 (.value(R1[7:4]));  // open: dp
  Hex_Digit_Display hex_digit_display_14 (.value(R1[3:0]));  // open: dp
  Hex_Digit_Display hex_digit_display_15 (.value(INDEX[7:4]));  // open: dp
  Hex_Digit_Display hex_digit_display_16 (.value(INDEX[3:0]));  // open: dp
  Hex_Digit_Display hex_digit_display_17 (.value(R2[15:12]));  // open: dp
  Hex_Digit_Display hex_digit_display_18 (.value(FPU[15:12]));  // open: dp
  Hex_Digit_Display hex_digit_display_19 (.value(R2[11:8]));  // open: dp
  Hex_Digit_Display hex_digit_display_20 (.value(R2[7:4]));  // open: dp
  Hex_Digit_Display hex_digit_display_21 (.value(FPU[11:8]));  // open: dp
  Hex_Digit_Display hex_digit_display_22 (.value(FPU[7:4]));  // open: dp
  Hex_Digit_Display hex_digit_display_23 (.value(R2[3:0]));  // open: dp
  Hex_Digit_Display hex_digit_display_24 (.value(FPU[3:0]));  // open: dp
  Hex_Digit_Display hex_digit_display_25 (.value(R3[15:12]));  // open: dp
  Hex_Digit_Display hex_digit_display_26 (.value(R3[11:8]));  // open: dp
  Hex_Digit_Display hex_digit_display_27 (.value(IAR[15:12]));  // open: dp
  Hex_Digit_Display hex_digit_display_28 (.value(IAR[11:8]));  // open: dp
  Hex_Digit_Display hex_digit_display_29 (.value(R3[7:4]));  // open: dp
  Hex_Digit_Display hex_digit_display_30 (.value(R3[3:0]));  // open: dp
  Hex_Digit_Display hex_digit_display_31 (.value(IAR[7:4]));  // open: dp
  Hex_Digit_Display hex_digit_display_32 (.value(IAR[3:0]));  // open: dp
  Hex_Digit_Display hex_digit_display_33 (.value(R4[15:12]));  // open: dp
  Hex_Digit_Display hex_digit_display_34 (.value(IR[15:12]));  // open: dp
  Hex_Digit_Display hex_digit_display_35 (.value(R4[11:8]));  // open: dp
  Hex_Digit_Display hex_digit_display_36 (.value(R4[7:4]));  // open: dp
  Hex_Digit_Display hex_digit_display_37 (.value(IR[11:8]));  // open: dp
  Hex_Digit_Display hex_digit_display_38 (.value(IR[7:4]));  // open: dp
  CPU_MOTHERBOARD cpu_motherboard_1 (
    .IN2(IN2), .IN3(IN3), .W(W), .CLK_IN(CLKIN), .r(r), .IN1(IN1), .R0(R0), .R1(R1), .R2(R2), .R3(R3),
    .IR(IR), .IAR(IAR), .SP(SP), .OUT1(OUT1), .OUT3(Y1), .KYB_CLK(KYB_CLK), .OUT2(OUT2), .out_24(OUT3),
    .out_26(X1), .CLKL(CLKL), .CLKE(CLKE), .CLKS(CLKS), .END(END), .FLAGS(FLAGS), .DIS_CLK(DIS_CLK),
    .INDEX(INDEX), .FPU(FPU), .R4(R4), .R5(R5), .R6_TEMP(R6_TEMP));
  Hex_Digit_Display hex_digit_display_39 (.value(R4[3:0]));  // open: dp
  Hex_Digit_Display hex_digit_display_40 (.value(IR[3:0]));  // open: dp
  LED led_1 (.in(FLAGS[4]));
  Hex_Digit_Display hex_digit_display_41 (.value(R5[15:12]));  // open: dp
  Hex_Digit_Display hex_digit_display_42 (.value(R5[11:8]));  // open: dp
  Hex_Digit_Display hex_digit_display_43 (.value(R6_TEMP[15:12]));  // open: dp
  Hex_Digit_Display hex_digit_display_44 (.value(R6_TEMP[11:8]));  // open: dp
  LED led_2 (.in(FLAGS[3]));
  LED led_3 (.in(FLAGS[2]));
  Hex_Digit_Display hex_digit_display_45 (.value(R5[7:4]));  // open: dp
  Hex_Digit_Display hex_digit_display_46 (.value(R5[3:0]));  // open: dp
  Hex_Digit_Display hex_digit_display_47 (.value(R6_TEMP[7:4]));  // open: dp
  Hex_Digit_Display hex_digit_display_48 (.value(R6_TEMP[3:0]));  // open: dp
  LED led_4 (.in(FLAGS[1]));
  LED led_5 (.in(FLAGS[0]));
  Button RESET (.out(r));
  LED #(.active("false")) led_6 (.in(END));
  Clock CLK (.out(CLKIN));
  Button CLR (.out(CLR_out));
  and and_1 (and_1_out, EN, TS);
  // Pins of 7 and 8 bits meet at OUT1
  // Pins of 7 and 8 bits meet at IN1

  // Notes on the sheet:
  //   DISPLAY
  //   KEYBOARD
  //   RO
  //   SP
  //   R1
  //   INDEX
  //   R2
  //   FPU
  //   GRAPHICS
  //   REGISTERS
  //   R3
  //   IAR
  //   COMPUTER
  //   R4
  //   IR
  //   Ci
  //   FLAGS
  //   Co
  //   A>B
  //   0
  //   1
  //   0
  //   R5
  //   R6 _TEMP
  //   A=B
  //   Z
  //   CONTROL
endmodule

module CPU_MEM_1 (
  input  in_1,
  input  in_2,
  input  r,
  output out_4
);

  wire controlled_buffer_1_out, nand_1_out, nand_2_out, nand_4_out, not_1_out, or_1_out;

  assign controlled_buffer_1_out = r ? 1'b0 : 1'bz;  // Controlled_Buffer controlled_buffer_1
  assign controlled_buffer_1_out = not_1_out ? in_1 : 1'bz;  // Controlled_Buffer controlled_buffer_2
  not not_1 (not_1_out, r);
  or or_1 (or_1_out, in_2, r);
  nand nand_1 (nand_1_out, controlled_buffer_1_out, or_1_out);
  nand nand_2 (nand_2_out, nand_1_out, or_1_out);
  nand nand_3 (out_4, nand_1_out, nand_4_out);
  nand nand_4 (nand_4_out, out_4, nand_2_out);
endmodule

module CPU_MEM_16 (
  input  [15:0] in_1,
  input  r,
  input  s,
  output [15:0] out_4
);

  CPU_MEM_1 cpu_mem_1_1 (.in_1(in_1[0]), .in_2(s), .r(r), .out_4(out_4[0]));
  CPU_MEM_1 cpu_mem_1_2 (.in_1(in_1[1]), .in_2(s), .r(r), .out_4(out_4[1]));
  CPU_MEM_1 cpu_mem_1_3 (.in_1(in_1[2]), .in_2(s), .r(r), .out_4(out_4[2]));
  CPU_MEM_1 cpu_mem_1_4 (.in_1(in_1[3]), .in_2(s), .r(r), .out_4(out_4[3]));
  CPU_MEM_1 cpu_mem_1_5 (.in_1(in_1[4]), .in_2(s), .r(r), .out_4(out_4[4]));
  CPU_MEM_1 cpu_mem_1_6 (.in_1(in_1[5]), .in_2(s), .r(r), .out_4(out_4[5]));
  CPU_MEM_1 cpu_mem_1_7 (.in_1(in_1[6]), .in_2(s), .r(r), .out_4(out_4[6]));
  CPU_MEM_1 cpu_mem_1_8 (.in_1(in_1[7]), .in_2(s), .r(r), .out_4(out_4[7]));
  CPU_MEM_1 cpu_mem_1_9 (.in_1(in_1[8]), .in_2(s), .r(r), .out_4(out_4[8]));
  CPU_MEM_1 cpu_mem_1_10 (.in_1(in_1[9]), .in_2(s), .r(r), .out_4(out_4[9]));
  CPU_MEM_1 cpu_mem_1_11 (.in_1(in_1[10]), .in_2(s), .r(r), .out_4(out_4[10]));
  CPU_MEM_1 cpu_mem_1_12 (.in_1(in_1[11]), .in_2(s), .r(r), .out_4(out_4[11]));
  CPU_MEM_1 cpu_mem_1_13 (.in_1(in_1[12]), .in_2(s), .r(r), .out_4(out_4[12]));
  CPU_MEM_1 cpu_mem_1_14 (.in_1(in_1[13]), .in_2(s), .r(r), .out_4(out_4[13]));
  CPU_MEM_1 cpu_mem_1_15 (.in_1(in_1[14]), .in_2(s), .r(r), .out_4(out_4[14]));
  CPU_MEM_1 cpu_mem_1_16 (.in_1(in_1[15]), .in_2(s), .r(r), .out_4(out_4[15]));
endmodule

module CPU_ENABLE_16 (
  input  [15:0] in_1,
  input  in_2,
  output [15:0] out_3
);

  wire and_1_out, and_2_out, and_3_out, and_4_out, and_5_out, and_6_out, and_7_out, and_8_out, and_9_out,
       and_10_out, and_11_out, and_12_out, and_13_out, and_14_out, and_15_out, and_16_out;

  and and_1 (and_1_out, in_1[0], in_2);
  and and_2 (and_2_out, in_1[1], in_2);
  and and_3 (and_3_out, in_1[2], in_2);
  and and_4 (and_4_out, in_1[3], in_2);
  and and_5 (and_5_out, in_1[4], in_2);
  and and_6 (and_6_out, in_1[5], in_2);
  and and_7 (and_7_out, in_1[6], in_2);
  and and_8 (and_8_out, in_1[7], in_2);
  and and_9 (and_9_out, in_1[8], in_2);
  and and_10 (and_10_out, in_1[9], in_2);
  and and_11 (and_11_out, in_1[10], in_2);
  and and_12 (and_12_out, in_1[11], in_2);
  and and_13 (and_13_out, in_1[12], in_2);
  and and_14 (and_14_out, in_1[13], in_2);
  and and_15 (and_15_out, in_1[14], in_2);
  and and_16 (and_16_out, in_1[15], in_2);
  assign out_3[0] = in_2 ? and_1_out : 1'bz;  // Controlled_Buffer controlled_buffer_1
  assign out_3[1] = in_2 ? and_2_out : 1'bz;  // Controlled_Buffer controlled_buffer_2
  assign out_3[2] = in_2 ? and_3_out : 1'bz;  // Controlled_Buffer controlled_buffer_3
  assign out_3[3] = in_2 ? and_4_out : 1'bz;  // Controlled_Buffer controlled_buffer_4
  assign out_3[4] = in_2 ? and_5_out : 1'bz;  // Controlled_Buffer controlled_buffer_5
  assign out_3[5] = in_2 ? and_6_out : 1'bz;  // Controlled_Buffer controlled_buffer_6
  assign out_3[6] = in_2 ? and_7_out : 1'bz;  // Controlled_Buffer controlled_buffer_7
  assign out_3[7] = in_2 ? and_8_out : 1'bz;  // Controlled_Buffer controlled_buffer_8
  assign out_3[8] = in_2 ? and_9_out : 1'bz;  // Controlled_Buffer controlled_buffer_9
  assign out_3[9] = in_2 ? and_10_out : 1'bz;  // Controlled_Buffer controlled_buffer_10
  assign out_3[10] = in_2 ? and_11_out : 1'bz;  // Controlled_Buffer controlled_buffer_11
  assign out_3[11] = in_2 ? and_12_out : 1'bz;  // Controlled_Buffer controlled_buffer_12
  assign out_3[12] = in_2 ? and_13_out : 1'bz;  // Controlled_Buffer controlled_buffer_13
  assign out_3[13] = in_2 ? and_14_out : 1'bz;  // Controlled_Buffer controlled_buffer_14
  assign out_3[14] = in_2 ? and_15_out : 1'bz;  // Controlled_Buffer controlled_buffer_15
  assign out_3[15] = in_2 ? and_16_out : 1'bz;  // Controlled_Buffer controlled_buffer_16
endmodule

module CPU_REGISTER_16 (
  input  [15:0] i,
  input  r,
  input  s,
  input  e,
  output [15:0] REG,
  output [15:0] L_0_5c1f849d
);

  wire [15:0] cpu_enable_16_1_out_3;

  CPU_MEM_16 cpu_mem_16_1 (.in_1(i), .r(r), .s(s), .out_4(REG));
  CPU_ENABLE_16 cpu_enable_16_1 (.in_1(REG), .in_2(e), .out_3(cpu_enable_16_1_out_3));
  assign L_0_5c1f849d = e ? cpu_enable_16_1_out_3 : 16'bz;  // Controlled_Buffer controlled_buffer_1
endmodule

module CPU_DECODER_4x16 (
  input  [3:0] in_1,
  output L,
  output out_3,
  output out_4,
  output out_5,
  output out_6,
  output out_7,
  output out_8,
  output out_9,
  output out_10,
  output out_11,
  output out_12,
  output out_13,
  output out_14,
  output out_15,
  output out_16,
  output M
);

  wire not_1_out, not_2_out, not_3_out, not_4_out;

  not not_1 (not_1_out, in_1[0]);
  not not_2 (not_2_out, in_1[1]);
  not not_3 (not_3_out, in_1[2]);
  not not_4 (not_4_out, in_1[3]);
  and and_1 (L, not_4_out, not_3_out, not_2_out, not_1_out);
  and and_2 (out_3, not_4_out, not_3_out, not_2_out, in_1[0]);
  and and_3 (out_4, not_4_out, not_3_out, in_1[1], not_1_out);
  and and_4 (out_5, not_4_out, not_3_out, in_1[1], in_1[0]);
  and and_5 (out_6, not_4_out, in_1[2], not_2_out, not_1_out);
  and and_6 (out_7, not_4_out, in_1[2], not_2_out, in_1[0]);
  and and_7 (out_8, not_4_out, in_1[2], in_1[1], not_1_out);
  and and_8 (out_9, not_4_out, in_1[2], in_1[1], in_1[0]);
  and and_9 (out_10, in_1[3], not_3_out, not_2_out, not_1_out);
  and and_10 (out_11, in_1[3], not_3_out, not_2_out, in_1[0]);
  and and_11 (out_12, in_1[3], not_3_out, in_1[1], not_1_out);
  and and_12 (out_13, in_1[3], not_3_out, in_1[1], in_1[0]);
  and and_13 (out_14, in_1[3], in_1[2], not_2_out, not_1_out);
  and and_14 (out_15, in_1[3], in_1[2], not_2_out, in_1[0]);
  and and_15 (out_16, in_1[3], in_1[2], in_1[1], not_1_out);
  and and_16 (M, in_1[3], in_1[2], in_1[1], in_1[0]);
endmodule

module CPU_REG_BYTE (
  input  [7:0] i,
  input  r,
  input  h,
  input  v,
  input  s,
  input  e,
  output [7:0] o,
  output [7:0] op
);

  wire and_1_out, and_2_out, and_3_out;
  wire [7:0] cpu_register_16_1_p6;

  and and_1 (and_1_out, h, v);
  and and_2 (and_2_out, and_1_out, s);
  and and_3 (and_3_out, and_1_out, e);
  // CPU_REGISTER_16 cpu_register_16_1: pin names not known; wires that end beside it: op, i, r, and_2_out, and_3_out, cpu_register_16_1_p6
  assign o = and_3_out ? cpu_register_16_1_p6 : 8'bz;  // Controlled_Buffer controlled_buffer_1
endmodule

module CPU_RAM_256 (
  input  r,
  input  [7:0] i,
  input  sa,
  input  [7:0] address,
  input  s,
  input  e,
  output [7:0] o,
  output [7:0] L_15_ad706d78,
  output [7:0] L_14_1024af5c,
  output [7:0] L_13_95069b4f,
  output [7:0] L_12_977d224a,
  output [7:0] L_11_11cac541,
  output [7:0] L_10_c5a8d897,
  output [7:0] L_9_41cebac5,
  output [7:0] L_8_d696b581,
  output [7:0] L_7_259d2eda,
  output [7:0] L_6_f477f93a,
  output [7:0] L_5_abe02a5b,
  output [7:0] L_4_4d692181,
  output [7:0] out_20,
  output [7:0] L_2_1ea30b77,
  output [7:0] L_1_b91444db,
  output [7:0] L_0_5c1f849d,
  output [7:0] L_31_156a63a1,
  output [7:0] L_30_c69d1e56,
  output [7:0] L_29_3ddb3c02,
  output [7:0] L_28_ccb5c83a,
  output [7:0] L_27_815ff803,
  output [7:0] L_26_3f41498e,
  output [7:0] L_25_2ce4f69c,
  output [7:0] L_24_028bd87a,
  output [7:0] L_23_94ca31e3,
  output [7:0] L_22_e3a6b9ce,
  output [7:0] L_21_02550864,
  output [7:0] L_20_f8652bf4,
  output [7:0] L_19_575d6bd7,
  output [7:0] L_18_7afa59f3,
  output [7:0] L_17_d1dc3eac,
  output [7:0] L_16_55794754,
  output [7:0] L_47_6fe5d602,
  output [7:0] L_46_9037878a,
  output [7:0] L_45_15c95849,
  output [7:0] L_44_755bc55f,
  output [7:0] L_43_c3b6d07c,
  output [7:0] L_42_e66f9d03,
  output [7:0] L_41_b74b1bdb,
  output [7:0] L_40_55c6a7f1,
  output [7:0] L_39_10ebac1e,
  output [7:0] L_38_5524d693,
  output [7:0] L_37_22a518f3,
  output [7:0] L_36_24a88140,
  output [7:0] L_35_34e425c9,
  output [7:0] L_34_fc51ff66,
  output [7:0] L_33_0e9a6c8e,
  output [7:0] L_32_3d63d3e9,
  output [7:0] L_63_b8ad389e,
  output [7:0] L_62_b3a2e3fd,
  output [7:0] L_61_d2a3d6cd,
  output [7:0] L_60_44546aba,
  output [7:0] L_59_8c086c19,
  output [7:0] L_58_0c5141ff,
  output [7:0] L_57_0f2507a8,
  output [7:0] L_56_ef77dc34,
  output [7:0] L_55_78950a6b,
  output [7:0] L_54_578b39e6,
  output [7:0] L_53_a28675a9,
  output [7:0] L_52_3bc4f444,
  output [7:0] L_51_eb6257e4,
  output [7:0] L_50_d2758f01,
  output [7:0] L_49_946bf74f,
  output [7:0] L_48_82b32e2a,
  output [7:0] L_79_8403bfd3,
  output [7:0] L_78_b94b47f7,
  output [7:0] L_77_25f4e05f,
  output [7:0] L_76_88476748,
  output [7:0] L_75_24619258,
  output [7:0] L_74_585ffe22,
  output [7:0] L_73_ddbbd28b,
  output [7:0] L_72_39c238b0,
  output [7:0] L_71_5b500dee,
  output [7:0] L_70_c09cf2ba,
  output [7:0] L_69_92ff2a4c,
  output [7:0] L_68_6960ef71,
  output [7:0] L_67_1f7a3999,
  output [7:0] L_66_1b20d148,
  output [7:0] L_65_6efbe4b3,
  output [7:0] L_64_ecf914bb,
  output [7:0] L_95_6512fe2e,
  output [7:0] L_94_fbda1007,
  output [7:0] L_93_76d13e06,
  output [7:0] L_92_3c23ad19,
  output [7:0] L_91_a710f268,
  output [7:0] L_90_e6684e30,
  output [7:0] L_89_731f133b,
  output [7:0] L_88_d0c7e292,
  output [7:0] L_87_57dc3f4b,
  output [7:0] L_86_d8beac51,
  output [7:0] L_85_549e2dd5,
  output [7:0] L_84_3272caa9,
  output [7:0] L_83_03a2b264,
  output [7:0] L_82_5190c9a8,
  output [7:0] L_81_1a1a38e7,
  output [7:0] L_80_2f0332ca,
  output [7:0] L_111_fae876db,
  output [7:0] L_110_67c157ec,
  output [7:0] L_109_e6bc2896,
  output [7:0] L_108_06754787,
  output [7:0] L_107_99897b65,
  output [7:0] L_106_bfb6d62f,
  output [7:0] L_105_d7d09b45,
  output [7:0] L_104_94ff6a6e,
  output [7:0] L_103_4d73e307,
  output [7:0] L_102_a9d73f14,
  output [7:0] L_101_848d6d95,
  output [7:0] L_100_a50e79c4,
  output [7:0] L_99_1605b5fb,
  output [7:0] L_98_6862fba1,
  output [7:0] L_97_2044529b,
  output [7:0] L_96_ab7d6c76,
  output [7:0] L_127_36bc8e9a,
  output [7:0] L_126_47cccd37,
  output [7:0] L_125_4d9638ec,
  output [7:0] L_124_7f15f756,
  output [7:0] L_123_ddf2dc58,
  output [7:0] L_122_143bcd3a,
  output [7:0] L_121_3730566e,
  output [7:0] L_120_fb957baa,
  output [7:0] L_119_7ef0fc3f,
  output [7:0] L_118_67beb245,
  output [7:0] L_117_fda830c3,
  output [7:0] L_116_48d4ffce,
  output [7:0] L_115_9ff82399,
  output [7:0] L_114_c8508d86,
  output [7:0] L_113_c869e249,
  output [7:0] L_112_66133eac,
  output [7:0] L_143_d47b5445,
  output [7:0] L_142_dff9f878,
  output [7:0] L_141_5ad63d84,
  output [7:0] L_140_e1a95fd0,
  output [7:0] L_139_eae45297,
  output [7:0] L_138_05725277,
  output [7:0] L_137_6e77535b,
  output [7:0] L_136_eabe134b,
  output [7:0] L_135_3b78403a,
  output [7:0] L_134_42fe3663,
  output [7:0] L_133_fccf8925,
  output [7:0] L_132_60bddf1f,
  output [7:0] L_131_4c1700d0,
  output [7:0] L_130_2cb406c6,
  output [7:0] L_129_b261d5f4,
  output [7:0] L_128_98843eb3,
  output [7:0] L_159_a86c72b5,
  output [7:0] L_158_147a73cc,
  output [7:0] L_157_ad2d5125,
  output [7:0] L_156_d45b8887,
  output [7:0] L_155_07d9e508,
  output [7:0] L_154_6ec9f278,
  output [7:0] L_153_10b77365,
  output [7:0] L_152_49acf9e5,
  output [7:0] L_151_085305e2,
  output [7:0] L_150_2849742c,
  output [7:0] L_149_6af5f21c,
  output [7:0] L_148_cc694576,
  output [7:0] L_147_dbbc7c10,
  output [7:0] L_146_984ad7ab,
  output [7:0] L_145_2ccf32d2,
  output [7:0] L_144_f0390f9a,
  output [7:0] L_175_73e96560,
  output [7:0] L_174_5b8ac4de,
  output [7:0] L_173_97570bde,
  output [7:0] L_172_8624c500,
  output [7:0] L_171_bf8c4fbb,
  output [7:0] L_170_9f554669,
  output [7:0] L_169_52386ece,
  output [7:0] L_168_f24e050e,
  output [7:0] L_167_0356249c,
  output [7:0] L_166_7fb580b8,
  output [7:0] L_165_d4e84403,
  output [7:0] L_164_588b9d2d,
  output [7:0] L_163_71990fdb,
  output [7:0] L_162_495b1a62,
  output [7:0] L_161_d08bfc9e,
  output [7:0] L_160_58ec8ce7,
  output [7:0] L_191_bd3a36f5,
  output [7:0] L_190_b7e6c28b,
  output [7:0] L_189_a1b47a77,
  output [7:0] L_188_2504910e,
  output [7:0] L_187_1f89ef21,
  output [7:0] L_186_9a405dd5,
  output [7:0] L_185_c2db7a30,
  output [7:0] L_184_17cfedd4,
  output [7:0] L_183_50847562,
  output [7:0] L_182_ab4227ad,
  output [7:0] L_181_001a9247,
  output [7:0] L_180_902375d6,
  output [7:0] L_179_fe58efa3,
  output [7:0] L_178_ff060783,
  output [7:0] L_177_ac914753,
  output [7:0] L_176_a0b11023,
  output [7:0] L_207_2339098b,
  output [7:0] L_206_b4c03dfe,
  output [7:0] L_205_8faab5d2,
  output [7:0] L_204_a7861f87,
  output [7:0] L_203_a8c39f6c,
  output [7:0] L_202_242d9594,
  output [7:0] L_201_1d2474bb,
  output [7:0] L_200_e602103d,
  output [7:0] L_199_bf24e250,
  output [7:0] L_198_2c87bdd1,
  output [7:0] L_197_956b7378,
  output [7:0] L_196_f75650f4,
  output [7:0] L_195_a976e483,
  output [7:0] L_194_b0343b4e,
  output [7:0] L_193_9e87d312,
  output [7:0] L_192_562a1697,
  output [7:0] L_223_7315f69d,
  output [7:0] L_222_6be29a99,
  output [7:0] L_221_0c4aa36a,
  output [7:0] L_220_b073b480,
  output [7:0] L_219_0adcfc14,
  output [7:0] L_218_6ec02a7a,
  output [7:0] L_217_6fe273b5,
  output [7:0] L_216_4bc9e3e5,
  output [7:0] L_215_5860435c,
  output [7:0] L_214_a6330ace,
  output [7:0] L_213_c5f10245,
  output [7:0] L_212_6087147a,
  output [7:0] L_211_5d26a315,
  output [7:0] L_210_93d8ec3c,
  output [7:0] L_209_83954787,
  output [7:0] L_208_cdb768a8,
  output [7:0] L_239_ded08ce8,
  output [7:0] L_238_f693b788,
  output [7:0] L_237_60e138df,
  output [7:0] L_236_b35427d6,
  output [7:0] L_235_13495a01,
  output [7:0] L_234_44b4ec39,
  output [7:0] L_233_e746773c,
  output [7:0] L_232_59dbde06,
  output [7:0] L_231_a36fef75,
  output [7:0] L_230_eac81f8e,
  output [7:0] L_229_87c6c7fa,
  output [7:0] L_228_3a2cdbe1,
  output [7:0] L_227_bed4bf61,
  output [7:0] L_226_88847811,
  output [7:0] L_225_b6925578,
  output [7:0] L_224_2cf65921,
  output [7:0] L_255_a242b549,
  output [7:0] L_254_f83ca4ac,
  output [7:0] L_253_37d8268e,
  output [7:0] L_252_9d8fae95,
  output [7:0] L_251_c363829a,
  output [7:0] L_250_260a1e1e,
  output [7:0] L_249_ef76f4d3,
  output [7:0] L_248_bd8cab2b,
  output [7:0] L_247_cde78628,
  output [7:0] L_246_3c0a0c8d,
  output [7:0] L_245_7d3cc3ed,
  output [7:0] L_244_071ec77e,
  output [7:0] L_243_8d097e4a,
  output [7:0] L_242_4675a6d4,
  output [7:0] L_241_ec1bb207,
  output [7:0] L_240_5e7f239c
);

  wire cpu_decoder_4x16_1_l, cpu_decoder_4x16_1_m, cpu_decoder_4x16_1_out_3, cpu_decoder_4x16_1_out_4,
       cpu_decoder_4x16_1_out_5, cpu_decoder_4x16_1_out_6, cpu_decoder_4x16_1_out_7,
       cpu_decoder_4x16_1_out_8, cpu_decoder_4x16_1_out_9, cpu_decoder_4x16_1_out_10,
       cpu_decoder_4x16_1_out_11, cpu_decoder_4x16_1_out_12, cpu_decoder_4x16_1_out_13,
       cpu_decoder_4x16_1_out_14, cpu_decoder_4x16_1_out_15, cpu_decoder_4x16_1_out_16, cpu_decoder_4x16_2_l,
       cpu_decoder_4x16_2_m, cpu_decoder_4x16_2_out_3, cpu_decoder_4x16_2_out_4, cpu_decoder_4x16_2_out_5,
       cpu_decoder_4x16_2_out_6, cpu_decoder_4x16_2_out_7, cpu_decoder_4x16_2_out_8,
       cpu_decoder_4x16_2_out_9, cpu_decoder_4x16_2_out_10, cpu_decoder_4x16_2_out_11,
       cpu_decoder_4x16_2_out_12, cpu_decoder_4x16_2_out_13, cpu_decoder_4x16_2_out_14,
       cpu_decoder_4x16_2_out_15, cpu_decoder_4x16_2_out_16;
  wire [7:0] cpu_mem_16_1_p4, cpu_reg_byte_1_o;

  // CPU_MEM_16 cpu_mem_16_1: pin names not known; wires that end beside it: address, r, sa, cpu_mem_16_1_p4
  CPU_DECODER_4x16 cpu_decoder_4x16_1 (
    .in_1(cpu_mem_16_1_p4[7:4]), .out_13(cpu_decoder_4x16_1_out_13), .out_14(cpu_decoder_4x16_1_out_14),
    .out_15(cpu_decoder_4x16_1_out_15), .out_16(cpu_decoder_4x16_1_out_16), .M(cpu_decoder_4x16_1_m),
    .L(cpu_decoder_4x16_1_l), .out_3(cpu_decoder_4x16_1_out_3), .out_4(cpu_decoder_4x16_1_out_4),
    .out_5(cpu_decoder_4x16_1_out_5), .out_6(cpu_decoder_4x16_1_out_6), .out_7(cpu_decoder_4x16_1_out_7),
    .out_8(cpu_decoder_4x16_1_out_8), .out_9(cpu_decoder_4x16_1_out_9), .out_10(cpu_decoder_4x16_1_out_10),
    .out_11(cpu_decoder_4x16_1_out_11), .out_12(cpu_decoder_4x16_1_out_12));
  assign o = e ? cpu_reg_byte_1_o : 8'bz;  // Controlled_Buffer controlled_buffer_1
  CPU_REG_BYTE cpu_reg_byte_1 (
    .h(cpu_decoder_4x16_1_l), .v(cpu_decoder_4x16_2_m), .r(r), .s(s), .e(e), .i(i), .op(L_15_ad706d78),
    .o(cpu_reg_byte_1_o));
  CPU_REG_BYTE cpu_reg_byte_2 (
    .h(cpu_decoder_4x16_1_out_3), .v(cpu_decoder_4x16_2_m), .r(r), .s(s), .e(e), .i(i), .op(L_31_156a63a1),
    .o(cpu_reg_byte_1_o));
  CPU_REG_BYTE cpu_reg_byte_3 (
    .h(cpu_decoder_4x16_1_out_4), .v(cpu_decoder_4x16_2_m), .r(r), .s(s), .e(e), .i(i), .op(L_47_6fe5d602),
    .o(cpu_reg_byte_1_o));
  CPU_REG_BYTE cpu_reg_byte_4 (
    .h(cpu_decoder_4x16_1_l), .v(cpu_decoder_4x16_2_out_16), .r(r), .s(s), .e(e), .i(i), .op(L_14_1024af5c),
    .o(cpu_reg_byte_1_o));
  CPU_REG_BYTE cpu_reg_byte_5 (
    .h(cpu_decoder_4x16_1_out_3), .v(cpu_decoder_4x16_2_out_16), .r(r), .s(s), .e(e), .i(i),
    .op(L_30_c69d1e56), .o(cpu_reg_byte_1_o));
  CPU_REG_BYTE cpu_reg_byte_6 (
    .h(cpu_decoder_4x16_1_out_4), .v(cpu_decoder_4x16_2_out_16), .r(r), .s(s), .e(e), .i(i),
    .op(L_46_9037878a), .o(cpu_reg_byte_1_o));
  CPU_REG_BYTE cpu_reg_byte_7 (
    .h(cpu_decoder_4x16_1_l), .v(cpu_decoder_4x16_2_out_15), .r(r), .s(s), .e(e), .i(i), .op(L_13_95069b4f),
    .o(cpu_reg_byte_1_o));
  CPU_REG_BYTE cpu_reg_byte_8 (
    .h(cpu_decoder_4x16_1_out_3), .v(cpu_decoder_4x16_2_out_15), .r(r), .s(s), .e(e), .i(i),
    .op(L_29_3ddb3c02), .o(cpu_reg_byte_1_o));
  CPU_REG_BYTE cpu_reg_byte_9 (
    .h(cpu_decoder_4x16_1_out_4), .v(cpu_decoder_4x16_2_out_15), .r(r), .s(s), .e(e), .i(i),
    .op(L_45_15c95849), .o(cpu_reg_byte_1_o));
  CPU_REG_BYTE cpu_reg_byte_10 (
    .h(cpu_decoder_4x16_1_l), .v(cpu_decoder_4x16_2_out_14), .r(r), .s(s), .e(e), .i(i), .op(L_12_977d224a),
    .o(cpu_reg_byte_1_o));
  CPU_REG_BYTE cpu_reg_byte_11 (
    .h(cpu_decoder_4x16_1_out_3), .v(cpu_decoder_4x16_2_out_14), .r(r), .s(s), .e(e), .i(i),
    .op(L_28_ccb5c83a), .o(cpu_reg_byte_1_o));
  CPU_REG_BYTE cpu_reg_byte_12 (
    .h(cpu_decoder_4x16_1_out_4), .v(cpu_decoder_4x16_2_out_14), .r(r), .s(s), .e(e), .i(i),
    .op(L_44_755bc55f), .o(cpu_reg_byte_1_o));
  CPU_REG_BYTE cpu_reg_byte_13 (
    .h(cpu_decoder_4x16_1_l), .v(cpu_decoder_4x16_2_out_13), .r(r), .s(s), .e(e), .i(i), .op(L_11_11cac541),
    .o(cpu_reg_byte_1_o));
  CPU_REG_BYTE cpu_reg_byte_14 (
    .h(cpu_decoder_4x16_1_out_3), .v(cpu_decoder_4x16_2_out_13), .r(r), .s(s), .e(e), .i(i),
    .op(L_27_815ff803), .o(cpu_reg_byte_1_o));
  CPU_REG_BYTE cpu_reg_byte_15 (
    .h(cpu_decoder_4x16_1_out_4), .v(cpu_decoder_4x16_2_out_13), .r(r), .s(s), .e(e), .i(i),
    .op(L_43_c3b6d07c), .o(cpu_reg_byte_1_o));
  CPU_REG_BYTE cpu_reg_byte_16 (
    .h(cpu_decoder_4x16_1_l), .v(cpu_decoder_4x16_2_out_12), .r(r), .s(s), .e(e), .i(i), .op(L_10_c5a8d897),
    .o(cpu_reg_byte_1_o));
  CPU_REG_BYTE cpu_reg_byte_17 (
    .h(cpu_decoder_4x16_1_out_3), .v(cpu_decoder_4x16_2_out_12), .r(r), .s(s), .e(e), .i(i),
    .op(L_26_3f41498e), .o(cpu_reg_byte_1_o));
  CPU_REG_BYTE cpu_reg_byte_18 (
    .h(cpu_decoder_4x16_1_out_4), .v(cpu_decoder_4x16_2_out_12), .r(r), .s(s), .e(e), .i(i),
    .op(L_42_e66f9d03), .o(cpu_reg_byte_1_o));
  CPU_REG_BYTE cpu_reg_byte_19 (
    .h(cpu_decoder_4x16_1_l), .v(cpu_decoder_4x16_2_out_11), .r(r), .s(s), .e(e), .i(i), .op(L_9_41cebac5),
    .o(cpu_reg_byte_1_o));
  CPU_REG_BYTE cpu_reg_byte_20 (
    .h(cpu_decoder_4x16_1_out_3), .v(cpu_decoder_4x16_2_out_11), .r(r), .s(s), .e(e), .i(i),
    .op(L_25_2ce4f69c), .o(cpu_reg_byte_1_o));
  CPU_REG_BYTE cpu_reg_byte_21 (
    .h(cpu_decoder_4x16_1_out_4), .v(cpu_decoder_4x16_2_out_11), .r(r), .s(s), .e(e), .i(i),
    .op(L_41_b74b1bdb), .o(cpu_reg_byte_1_o));
  CPU_REG_BYTE cpu_reg_byte_22 (
    .h(cpu_decoder_4x16_1_l), .v(cpu_decoder_4x16_2_out_10), .r(r), .s(s), .e(e), .i(i), .op(L_8_d696b581),
    .o(cpu_reg_byte_1_o));
  CPU_REG_BYTE cpu_reg_byte_23 (
    .h(cpu_decoder_4x16_1_out_3), .v(cpu_decoder_4x16_2_out_10), .r(r), .s(s), .e(e), .i(i),
    .op(L_24_028bd87a), .o(cpu_reg_byte_1_o));
  CPU_REG_BYTE cpu_reg_byte_24 (
    .h(cpu_decoder_4x16_1_out_4), .v(cpu_decoder_4x16_2_out_10), .r(r), .s(s), .e(e), .i(i),
    .op(L_40_55c6a7f1), .o(cpu_reg_byte_1_o));
  CPU_DECODER_4x16 cpu_decoder_4x16_2 (
    .in_1(cpu_mem_16_1_p4[3:0]), .out_13(cpu_decoder_4x16_2_out_13), .out_14(cpu_decoder_4x16_2_out_14),
    .out_15(cpu_decoder_4x16_2_out_15), .out_16(cpu_decoder_4x16_2_out_16), .M(cpu_decoder_4x16_2_m),
    .L(cpu_decoder_4x16_2_l), .out_3(cpu_decoder_4x16_2_out_3), .out_4(cpu_decoder_4x16_2_out_4),
    .out_5(cpu_decoder_4x16_2_out_5), .out_6(cpu_decoder_4x16_2_out_6), .out_7(cpu_decoder_4x16_2_out_7),
    .out_8(cpu_decoder_4x16_2_out_8), .out_9(cpu_decoder_4x16_2_out_9), .out_10(cpu_decoder_4x16_2_out_10),
    .out_11(cpu_decoder_4x16_2_out_11), .out_12(cpu_decoder_4x16_2_out_12));
  CPU_REG_BYTE cpu_reg_byte_25 (
    .h(cpu_decoder_4x16_1_l), .v(cpu_decoder_4x16_2_out_9), .r(r), .s(s), .e(e), .i(i), .op(L_7_259d2eda),
    .o(cpu_reg_byte_1_o));
  CPU_REG_BYTE cpu_reg_byte_26 (
    .h(cpu_decoder_4x16_1_out_3), .v(cpu_decoder_4x16_2_out_9), .r(r), .s(s), .e(e), .i(i),
    .op(L_23_94ca31e3), .o(cpu_reg_byte_1_o));
  CPU_REG_BYTE cpu_reg_byte_27 (
    .h(cpu_decoder_4x16_1_out_4), .v(cpu_decoder_4x16_2_out_9), .r(r), .s(s), .e(e), .i(i),
    .op(L_39_10ebac1e), .o(cpu_reg_byte_1_o));
  CPU_REG_BYTE cpu_reg_byte_28 (
    .h(cpu_decoder_4x16_1_l), .v(cpu_decoder_4x16_2_out_8), .r(r), .s(s), .e(e), .i(i), .op(L_6_f477f93a),
    .o(cpu_reg_byte_1_o));
  CPU_REG_BYTE cpu_reg_byte_29 (
    .h(cpu_decoder_4x16_1_out_3), .v(cpu_decoder_4x16_2_out_8), .r(r), .s(s), .e(e), .i(i),
    .op(L_22_e3a6b9ce), .o(cpu_reg_byte_1_o));
  CPU_REG_BYTE cpu_reg_byte_30 (
    .h(cpu_decoder_4x16_1_out_4), .v(cpu_decoder_4x16_2_out_8), .r(r), .s(s), .e(e), .i(i),
    .op(L_38_5524d693), .o(cpu_reg_byte_1_o));
  CPU_REG_BYTE cpu_reg_byte_31 (
    .h(cpu_decoder_4x16_1_l), .v(cpu_decoder_4x16_2_out_7), .r(r), .s(s), .e(e), .i(i), .op(L_5_abe02a5b),
    .o(cpu_reg_byte_1_o));
  CPU_REG_BYTE cpu_reg_byte_32 (
    .h(cpu_decoder_4x16_1_out_3), .v(cpu_decoder_4x16_2_out_7), .r(r), .s(s), .e(e), .i(i),
    .op(L_21_02550864), .o(cpu_reg_byte_1_o));
  CPU_REG_BYTE cpu_reg_byte_33 (
    .h(cpu_decoder_4x16_1_out_4), .v(cpu_decoder_4x16_2_out_7), .r(r), .s(s), .e(e), .i(i),
    .op(L_37_22a518f3), .o(cpu_reg_byte_1_o));
  CPU_REG_BYTE cpu_reg_byte_34 (
    .h(cpu_decoder_4x16_1_l), .v(cpu_decoder_4x16_2_out_6), .r(r), .s(s), .e(e), .i(i), .op(L_4_4d692181),
    .o(cpu_reg_byte_1_o));
  CPU_REG_BYTE cpu_reg_byte_35 (
    .h(cpu_decoder_4x16_1_out_3), .v(cpu_decoder_4x16_2_out_6), .r(r), .s(s), .e(e), .i(i),
    .op(L_20_f8652bf4), .o(cpu_reg_byte_1_o));
  CPU_REG_BYTE cpu_reg_byte_36 (
    .h(cpu_decoder_4x16_1_out_4), .v(cpu_decoder_4x16_2_out_6), .r(r), .s(s), .e(e), .i(i),
    .op(L_36_24a88140), .o(cpu_reg_byte_1_o));
  CPU_REG_BYTE cpu_reg_byte_37 (
    .h(cpu_decoder_4x16_1_l), .v(cpu_decoder_4x16_2_out_5), .r(r), .s(s), .e(e), .i(i), .op(out_20),
    .o(cpu_reg_byte_1_o));
  CPU_REG_BYTE cpu_reg_byte_38 (
    .h(cpu_decoder_4x16_1_out_3), .v(cpu_decoder_4x16_2_out_5), .r(r), .s(s), .e(e), .i(i),
    .op(L_19_575d6bd7), .o(cpu_reg_byte_1_o));
  CPU_REG_BYTE cpu_reg_byte_39 (
    .h(cpu_decoder_4x16_1_out_4), .v(cpu_decoder_4x16_2_out_5), .r(r), .s(s), .e(e), .i(i),
    .op(L_35_34e425c9), .o(cpu_reg_byte_1_o));
  CPU_REG_BYTE cpu_reg_byte_40 (
    .h(cpu_decoder_4x16_1_l), .v(cpu_decoder_4x16_2_out_4), .r(r), .s(s), .e(e), .i(i), .op(L_2_1ea30b77),
    .o(cpu_reg_byte_1_o));
  CPU_REG_BYTE cpu_reg_byte_41 (
    .h(cpu_decoder_4x16_1_out_3), .v(cpu_decoder_4x16_2_out_4), .r(r), .s(s), .e(e), .i(i),
    .op(L_18_7afa59f3), .o(cpu_reg_byte_1_o));
  CPU_REG_BYTE cpu_reg_byte_42 (
    .h(cpu_decoder_4x16_1_out_4), .v(cpu_decoder_4x16_2_out_4), .r(r), .s(s), .e(e), .i(i),
    .op(L_34_fc51ff66), .o(cpu_reg_byte_1_o));
  CPU_REG_BYTE cpu_reg_byte_43 (
    .h(cpu_decoder_4x16_1_l), .v(cpu_decoder_4x16_2_out_3), .r(r), .s(s), .e(e), .i(i), .op(L_1_b91444db),
    .o(cpu_reg_byte_1_o));
  CPU_REG_BYTE cpu_reg_byte_44 (
    .h(cpu_decoder_4x16_1_out_3), .v(cpu_decoder_4x16_2_out_3), .r(r), .s(s), .e(e), .i(i),
    .op(L_17_d1dc3eac), .o(cpu_reg_byte_1_o));
  CPU_REG_BYTE cpu_reg_byte_45 (
    .h(cpu_decoder_4x16_1_out_4), .v(cpu_decoder_4x16_2_out_3), .r(r), .s(s), .e(e), .i(i),
    .op(L_33_0e9a6c8e), .o(cpu_reg_byte_1_o));
  CPU_REG_BYTE cpu_reg_byte_46 (
    .h(cpu_decoder_4x16_1_l), .v(cpu_decoder_4x16_2_l), .r(r), .s(s), .e(e), .i(i), .op(L_0_5c1f849d),
    .o(cpu_reg_byte_1_o));
  CPU_REG_BYTE cpu_reg_byte_47 (
    .h(cpu_decoder_4x16_1_out_3), .v(cpu_decoder_4x16_2_l), .r(r), .s(s), .e(e), .i(i), .op(L_16_55794754),
    .o(cpu_reg_byte_1_o));
  CPU_REG_BYTE cpu_reg_byte_48 (
    .h(cpu_decoder_4x16_1_out_4), .v(cpu_decoder_4x16_2_l), .r(r), .s(s), .e(e), .i(i), .op(L_32_3d63d3e9),
    .o(cpu_reg_byte_1_o));
  CPU_REG_BYTE cpu_reg_byte_49 (
    .h(cpu_decoder_4x16_1_out_5), .v(cpu_decoder_4x16_2_l), .r(r), .s(s), .e(e), .i(i), .op(L_48_82b32e2a),
    .o(cpu_reg_byte_1_o));
endmodule

module CPU_NOT (
  input  [15:0] i,
  output [15:0] out_2
);

  not not_1 (out_2[0], i[0]);
  not not_2 (out_2[1], i[1]);
  not not_3 (out_2[2], i[2]);
  not not_4 (out_2[3], i[3]);
  not not_5 (out_2[4], i[4]);
  not not_6 (out_2[5], i[5]);
  not not_7 (out_2[6], i[6]);
  not not_8 (out_2[7], i[7]);
  not not_9 (out_2[8], i[8]);
  not not_10 (out_2[9], i[9]);
  not not_11 (out_2[10], i[10]);
  not not_12 (out_2[11], i[11]);
  not not_13 (out_2[12], i[12]);
  not not_14 (out_2[13], i[13]);
  not not_15 (out_2[14], i[14]);
  not not_16 (out_2[15], i[15]);
endmodule

module CPU_AND (
  input  [15:0] a,
  input  [15:0] b,
  output [15:0] o
);

  and and_1 (o[0], a[0], b[0]);
  and and_2 (o[1], a[1], b[1]);
  and and_3 (o[2], a[2], b[2]);
  and and_4 (o[3], a[3], b[3]);
  and and_5 (o[4], a[4], b[4]);
  and and_6 (o[5], a[5], b[5]);
  and and_7 (o[6], a[6], b[6]);
  and and_8 (o[7], a[7], b[7]);
  and and_9 (o[8], a[8], b[8]);
  and and_10 (o[9], a[9], b[9]);
  and and_11 (o[10], a[10], b[10]);
  and and_12 (o[11], a[11], b[11]);
  and and_13 (o[12], a[12], b[12]);
  and and_14 (o[13], a[13], b[13]);
  and and_15 (o[14], a[14], b[14]);
  and and_16 (o[15], a[15], b[15]);
endmodule

module CPU_OR (
  input  [15:0] a,
  input  [15:0] b,
  output [15:0] L_0_5c1f849d
);

  or or_1 (L_0_5c1f849d[0], a[0], b[0]);
  or or_2 (L_0_5c1f849d[1], a[1], b[1]);
  or or_3 (L_0_5c1f849d[2], a[2], b[2]);
  or or_4 (L_0_5c1f849d[3], a[3], b[3]);
  or or_5 (L_0_5c1f849d[4], a[4], b[4]);
  or or_6 (L_0_5c1f849d[5], a[5], b[5]);
  or or_7 (L_0_5c1f849d[6], a[6], b[6]);
  or or_8 (L_0_5c1f849d[7], a[7], b[7]);
  or or_9 (L_0_5c1f849d[8], a[8], b[8]);
  or or_10 (L_0_5c1f849d[9], a[9], b[9]);
  or or_11 (L_0_5c1f849d[10], a[10], b[10]);
  or or_12 (L_0_5c1f849d[11], a[11], b[11]);
  or or_13 (L_0_5c1f849d[12], a[12], b[12]);
  or or_14 (L_0_5c1f849d[13], a[13], b[13]);
  or or_15 (L_0_5c1f849d[14], a[14], b[14]);
  or or_16 (L_0_5c1f849d[15], a[15], b[15]);
endmodule

module CPU_XOR_1 (
  input  a,
  input  b,
  output o
);

  wire nand_1_out, nand_2_out, not_1_out, not_2_out;

  not not_1 (not_1_out, a);
  not not_2 (not_2_out, b);
  nand nand_1 (nand_1_out, not_1_out, b);
  nand nand_2 (nand_2_out, a, not_2_out);
  nand nand_3 (o, nand_1_out, nand_2_out);
endmodule

module CPU_SHR (
  input  [15:0] i,
  input  r,
  input  shift_in_6fb471af,
  output shift_out_da4ee8f1,
  output [15:0] o
);

  wire [15:1] cpu_register_16_1_l_0_5c1f849d;

  CPU_REGISTER_16 cpu_register_16_1 (
    .i(i), .r(r), .s(1'b1), .e(1'b1), .L_0_5c1f849d({cpu_register_16_1_l_0_5c1f849d, shift_out_da4ee8f1}));  // open: REG
  CPU_REGISTER_16 cpu_register_16_2 (
    .i({shift_in_6fb471af, cpu_register_16_1_l_0_5c1f849d}), .r(r), .s(1'b1), .e(1'b1), .L_0_5c1f849d(o));  // open: REG
endmodule

module CPU_SHL (
  input  shift_in,
  input  [15:0] i,
  input  r,
  input  [15:0] r1,
  output [15:0] o,
  output shift_out
);

  wire [14:0] cpu_register_16_1_l_0_5c1f849d;

  CPU_REGISTER_16 cpu_register_16_1 (
    .i(i), .r(r), .s(1'b1), .e(1'b1), .L_0_5c1f849d({shift_out, cpu_register_16_1_l_0_5c1f849d}));  // open: REG
  CPU_REGISTER_16 cpu_register_16_2 (
    .i({cpu_register_16_1_l_0_5c1f849d, shift_in}), .r(r), .s(1'b1), .e(1'b1), .L_0_5c1f849d(o));  // open: REG
endmodule

module CPU_ADDER (
  input  a,
  input  b,
  input  carry_in_d14b9ec6,
  output sum,
  output carry_out_c1e17e93
);

  wire and_1_out, and_2_out, cpu_xor_1_1_o;

  CPU_XOR_1 cpu_xor_1_1 (.a(a), .b(b), .o(cpu_xor_1_1_o));
  and and_1 (and_1_out, carry_in_d14b9ec6, cpu_xor_1_1_o);
  and and_2 (and_2_out, a, b);
  CPU_XOR_1 cpu_xor_1_2 (.a(cpu_xor_1_1_o), .b(carry_in_d14b9ec6), .o(sum));
  or or_1 (carry_out_c1e17e93, and_1_out, and_2_out);
endmodule

module CPU_ADDER_8 (
  input  [15:0] a,
  input  [15:0] b,
  input  carry_in_d14b9ec6,
  output carry_out_c1e17e93,
  output [15:0] out_5
);

  wire cpu_adder_2_carry_out_c1e17e93, cpu_adder_3_carry_out_c1e17e93, cpu_adder_4_carry_out_c1e17e93,
       cpu_adder_5_carry_out_c1e17e93, cpu_adder_6_carry_out_c1e17e93, cpu_adder_7_carry_out_c1e17e93,
       cpu_adder_8_carry_out_c1e17e93, cpu_adder_9_carry_out_c1e17e93, cpu_adder_10_carry_out_c1e17e93,
       cpu_adder_11_carry_out_c1e17e93, cpu_adder_12_carry_out_c1e17e93, cpu_adder_13_carry_out_c1e17e93,
       cpu_adder_14_carry_out_c1e17e93, cpu_adder_15_carry_out_c1e17e93, cpu_adder_16_carry_out_c1e17e93;

  CPU_ADDER cpu_adder_1 (
    .carry_in_d14b9ec6(cpu_adder_2_carry_out_c1e17e93), .a(a[15]), .b(b[15]), .sum(out_5[15]),
    .carry_out_c1e17e93(carry_out_c1e17e93));
  CPU_ADDER cpu_adder_2 (
    .carry_in_d14b9ec6(cpu_adder_3_carry_out_c1e17e93), .a(a[14]), .b(b[14]), .sum(out_5[14]),
    .carry_out_c1e17e93(cpu_adder_2_carry_out_c1e17e93));
  CPU_ADDER cpu_adder_3 (
    .carry_in_d14b9ec6(cpu_adder_4_carry_out_c1e17e93), .a(a[13]), .b(b[13]), .sum(out_5[13]),
    .carry_out_c1e17e93(cpu_adder_3_carry_out_c1e17e93));
  CPU_ADDER cpu_adder_4 (
    .carry_in_d14b9ec6(cpu_adder_5_carry_out_c1e17e93), .a(a[12]), .b(b[12]), .sum(out_5[12]),
    .carry_out_c1e17e93(cpu_adder_4_carry_out_c1e17e93));
  CPU_ADDER cpu_adder_5 (
    .carry_in_d14b9ec6(cpu_adder_6_carry_out_c1e17e93), .a(a[11]), .b(b[11]), .sum(out_5[11]),
    .carry_out_c1e17e93(cpu_adder_5_carry_out_c1e17e93));
  CPU_ADDER cpu_adder_6 (
    .carry_in_d14b9ec6(cpu_adder_7_carry_out_c1e17e93), .a(a[10]), .b(b[10]), .sum(out_5[10]),
    .carry_out_c1e17e93(cpu_adder_6_carry_out_c1e17e93));
  CPU_ADDER cpu_adder_7 (
    .carry_in_d14b9ec6(cpu_adder_8_carry_out_c1e17e93), .a(a[9]), .b(b[9]), .sum(out_5[9]),
    .carry_out_c1e17e93(cpu_adder_7_carry_out_c1e17e93));
  CPU_ADDER cpu_adder_8 (
    .carry_in_d14b9ec6(cpu_adder_9_carry_out_c1e17e93), .a(a[8]), .b(b[8]), .sum(out_5[8]),
    .carry_out_c1e17e93(cpu_adder_8_carry_out_c1e17e93));
  CPU_ADDER cpu_adder_9 (
    .carry_in_d14b9ec6(cpu_adder_10_carry_out_c1e17e93), .a(a[7]), .b(b[7]), .sum(out_5[7]),
    .carry_out_c1e17e93(cpu_adder_9_carry_out_c1e17e93));
  CPU_ADDER cpu_adder_10 (
    .carry_in_d14b9ec6(cpu_adder_11_carry_out_c1e17e93), .a(a[6]), .b(b[6]), .sum(out_5[6]),
    .carry_out_c1e17e93(cpu_adder_10_carry_out_c1e17e93));
  CPU_ADDER cpu_adder_11 (
    .carry_in_d14b9ec6(cpu_adder_12_carry_out_c1e17e93), .a(a[5]), .b(b[5]), .sum(out_5[5]),
    .carry_out_c1e17e93(cpu_adder_11_carry_out_c1e17e93));
  CPU_ADDER cpu_adder_12 (
    .carry_in_d14b9ec6(cpu_adder_13_carry_out_c1e17e93), .a(a[4]), .b(b[4]), .sum(out_5[4]),
    .carry_out_c1e17e93(cpu_adder_12_carry_out_c1e17e93));
  CPU_ADDER cpu_adder_13 (
    .carry_in_d14b9ec6(cpu_adder_14_carry_out_c1e17e93), .a(a[3]), .b(b[3]), .sum(out_5[3]),
    .carry_out_c1e17e93(cpu_adder_13_carry_out_c1e17e93));
  CPU_ADDER cpu_adder_14 (
    .carry_in_d14b9ec6(cpu_adder_15_carry_out_c1e17e93), .a(a[2]), .b(b[2]), .sum(out_5[2]),
    .carry_out_c1e17e93(cpu_adder_14_carry_out_c1e17e93));
  CPU_ADDER cpu_adder_15 (
    .carry_in_d14b9ec6(cpu_adder_16_carry_out_c1e17e93), .a(a[1]), .b(b[1]), .sum(out_5[1]),
    .carry_out_c1e17e93(cpu_adder_15_carry_out_c1e17e93));
  CPU_ADDER cpu_adder_16 (
    .carry_in_d14b9ec6(carry_in_d14b9ec6), .a(a[0]), .b(b[0]), .sum(out_5[0]),
    .carry_out_c1e17e93(cpu_adder_16_carry_out_c1e17e93));
endmodule

module CPU_XOR_LE_1 (
  input  above_equal_afdd2708,
  input  a_larger_39a03663,
  input  a,
  input  b,
  output c,
  output equal,
  output a_large
);

  wire and_2_out, not_1_out;

  CPU_XOR_1 cpu_xor_1_1 (.a(a), .b(b), .o(c));
  not not_1 (not_1_out, c);
  and and_1 (equal, not_1_out, above_equal_afdd2708);
  and and_2 (and_2_out, above_equal_afdd2708, a, c);
  or or_1 (a_large, and_2_out, a_larger_39a03663);
endmodule

module CPU_XOR_LE_16 (
  input  [15:0] a,
  input  [15:0] b,
  output [15:0] out_3,
  output larger,
  output equal
);

  wire cpu_xor_le_1_1_a_large, cpu_xor_le_1_1_equal, cpu_xor_le_1_2_a_large, cpu_xor_le_1_2_equal,
       cpu_xor_le_1_3_a_large, cpu_xor_le_1_3_equal, cpu_xor_le_1_4_a_large, cpu_xor_le_1_4_equal,
       cpu_xor_le_1_5_a_large, cpu_xor_le_1_5_equal, cpu_xor_le_1_6_a_large, cpu_xor_le_1_6_equal,
       cpu_xor_le_1_7_a_large, cpu_xor_le_1_7_equal, cpu_xor_le_1_8_a_large, cpu_xor_le_1_8_equal,
       cpu_xor_le_1_9_a_large, cpu_xor_le_1_9_equal, cpu_xor_le_1_10_a_large, cpu_xor_le_1_10_equal,
       cpu_xor_le_1_11_a_large, cpu_xor_le_1_11_equal, cpu_xor_le_1_12_a_large, cpu_xor_le_1_12_equal,
       cpu_xor_le_1_13_a_large, cpu_xor_le_1_13_equal, cpu_xor_le_1_14_a_large, cpu_xor_le_1_14_equal,
       cpu_xor_le_1_15_a_large, cpu_xor_le_1_15_equal, undriven;

  CPU_XOR_LE_1 cpu_xor_le_1_1 (
    .a(a[15]), .b(b[15]), .above_equal_afdd2708(1'b1), .a_larger_39a03663(undriven),
    .equal(cpu_xor_le_1_1_equal), .a_large(cpu_xor_le_1_1_a_large), .c(out_3[0]));
  CPU_XOR_LE_1 cpu_xor_le_1_2 (
    .a(a[14]), .b(b[14]), .above_equal_afdd2708(cpu_xor_le_1_1_equal),
    .a_larger_39a03663(cpu_xor_le_1_1_a_large), .equal(cpu_xor_le_1_2_equal),
    .a_large(cpu_xor_le_1_2_a_large), .c(out_3[1]));
  CPU_XOR_LE_1 cpu_xor_le_1_3 (
    .a(a[13]), .b(b[13]), .above_equal_afdd2708(cpu_xor_le_1_2_equal),
    .a_larger_39a03663(cpu_xor_le_1_2_a_large), .equal(cpu_xor_le_1_3_equal),
    .a_large(cpu_xor_le_1_3_a_large), .c(out_3[2]));
  CPU_XOR_LE_1 cpu_xor_le_1_4 (
    .a(a[12]), .b(b[12]), .above_equal_afdd2708(cpu_xor_le_1_3_equal),
    .a_larger_39a03663(cpu_xor_le_1_3_a_large), .equal(cpu_xor_le_1_4_equal),
    .a_large(cpu_xor_le_1_4_a_large), .c(out_3[3]));
  CPU_XOR_LE_1 cpu_xor_le_1_5 (
    .a(a[11]), .b(b[11]), .above_equal_afdd2708(cpu_xor_le_1_4_equal),
    .a_larger_39a03663(cpu_xor_le_1_4_a_large), .equal(cpu_xor_le_1_5_equal),
    .a_large(cpu_xor_le_1_5_a_large), .c(out_3[4]));
  CPU_XOR_LE_1 cpu_xor_le_1_6 (
    .a(a[10]), .b(b[10]), .above_equal_afdd2708(cpu_xor_le_1_5_equal),
    .a_larger_39a03663(cpu_xor_le_1_5_a_large), .equal(cpu_xor_le_1_6_equal),
    .a_large(cpu_xor_le_1_6_a_large), .c(out_3[5]));
  CPU_XOR_LE_1 cpu_xor_le_1_7 (
    .a(a[9]), .b(b[9]), .above_equal_afdd2708(cpu_xor_le_1_6_equal),
    .a_larger_39a03663(cpu_xor_le_1_6_a_large), .equal(cpu_xor_le_1_7_equal),
    .a_large(cpu_xor_le_1_7_a_large), .c(out_3[6]));
  CPU_XOR_LE_1 cpu_xor_le_1_8 (
    .a(a[8]), .b(b[8]), .above_equal_afdd2708(cpu_xor_le_1_7_equal),
    .a_larger_39a03663(cpu_xor_le_1_7_a_large), .equal(cpu_xor_le_1_8_equal),
    .a_large(cpu_xor_le_1_8_a_large), .c(out_3[7]));
  CPU_XOR_LE_1 cpu_xor_le_1_9 (
    .a(a[7]), .b(b[7]), .above_equal_afdd2708(cpu_xor_le_1_8_equal),
    .a_larger_39a03663(cpu_xor_le_1_8_a_large), .equal(cpu_xor_le_1_9_equal),
    .a_large(cpu_xor_le_1_9_a_large), .c(out_3[8]));
  CPU_XOR_LE_1 cpu_xor_le_1_10 (
    .a(a[6]), .b(b[6]), .above_equal_afdd2708(cpu_xor_le_1_9_equal),
    .a_larger_39a03663(cpu_xor_le_1_9_a_large), .equal(cpu_xor_le_1_10_equal),
    .a_large(cpu_xor_le_1_10_a_large), .c(out_3[9]));
  CPU_XOR_LE_1 cpu_xor_le_1_11 (
    .a(a[5]), .b(b[5]), .above_equal_afdd2708(cpu_xor_le_1_10_equal),
    .a_larger_39a03663(cpu_xor_le_1_10_a_large), .equal(cpu_xor_le_1_11_equal),
    .a_large(cpu_xor_le_1_11_a_large), .c(out_3[10]));
  CPU_XOR_LE_1 cpu_xor_le_1_12 (
    .a(a[4]), .b(b[4]), .above_equal_afdd2708(cpu_xor_le_1_11_equal),
    .a_larger_39a03663(cpu_xor_le_1_11_a_large), .equal(cpu_xor_le_1_12_equal),
    .a_large(cpu_xor_le_1_12_a_large), .c(out_3[11]));
  CPU_XOR_LE_1 cpu_xor_le_1_13 (
    .a(a[3]), .b(b[3]), .above_equal_afdd2708(cpu_xor_le_1_12_equal),
    .a_larger_39a03663(cpu_xor_le_1_12_a_large), .equal(cpu_xor_le_1_13_equal),
    .a_large(cpu_xor_le_1_13_a_large), .c(out_3[12]));
  CPU_XOR_LE_1 cpu_xor_le_1_14 (
    .a(a[2]), .b(b[2]), .above_equal_afdd2708(cpu_xor_le_1_13_equal),
    .a_larger_39a03663(cpu_xor_le_1_13_a_large), .equal(cpu_xor_le_1_14_equal),
    .a_large(cpu_xor_le_1_14_a_large), .c(out_3[13]));
  CPU_XOR_LE_1 cpu_xor_le_1_15 (
    .a(a[1]), .b(b[1]), .above_equal_afdd2708(cpu_xor_le_1_14_equal),
    .a_larger_39a03663(cpu_xor_le_1_14_a_large), .equal(cpu_xor_le_1_15_equal),
    .a_large(cpu_xor_le_1_15_a_large), .c(out_3[14]));
  CPU_XOR_LE_1 cpu_xor_le_1_16 (
    .a(a[0]), .b(b[0]), .above_equal_afdd2708(cpu_xor_le_1_15_equal),
    .a_larger_39a03663(cpu_xor_le_1_15_a_large), .equal(equal), .a_large(larger), .c(out_3[15]));
endmodule

module CPU_Z (
  input  [15:0] i,
  output o
);

  wire or_1_out;

  or or_1 (or_1_out, i[0], i[1], i[2], i[3], i[4], i[5], i[6], i[7], i[8], i[9], i[10], i[11], i[12], i[13], i[14], i[15]);
  not not_1 (o, or_1_out);
endmodule

module CPU_DECODER_3x8 (
  input  c,
  input  b,
  input  a,
  output [7:0] o
);

  wire not_1_out, not_2_out, not_3_out;

  not not_1 (not_1_out, a);
  not not_2 (not_2_out, b);
  not not_3 (not_3_out, c);
  and and_1 (o[0], not_3_out, not_2_out, not_1_out);
  and and_2 (o[1], not_3_out, not_2_out, a);
  and and_3 (o[2], not_3_out, b, not_1_out);
  and and_4 (o[3], not_3_out, b, a);
  and and_5 (o[4], c, not_2_out, not_1_out);
  and and_6 (o[5], c, not_2_out, a);
  and and_7 (o[6], c, b, not_1_out);
  and and_8 (o[7], c, b, a);

  // Notes on the sheet:
  //   msb
  //   lsb
endmodule

module CPU_E (
  input  [15:0] in_1,
  input  in_2,
  output [15:0] out_3
);

  wire and_1_out, and_2_out, and_3_out, and_4_out, and_5_out, and_6_out, and_7_out, and_8_out, and_9_out,
       and_10_out, and_11_out, and_12_out, and_13_out, and_14_out, and_15_out, and_16_out;

  and and_1 (and_1_out, in_1[0], in_2);
  assign out_3[0] = in_2 ? and_1_out : 1'bz;  // Controlled_Buffer controlled_buffer_1
  and and_2 (and_2_out, in_1[1], in_2);
  assign out_3[1] = in_2 ? and_2_out : 1'bz;  // Controlled_Buffer controlled_buffer_2
  and and_3 (and_3_out, in_1[2], in_2);
  assign out_3[2] = in_2 ? and_3_out : 1'bz;  // Controlled_Buffer controlled_buffer_3
  and and_4 (and_4_out, in_1[3], in_2);
  assign out_3[3] = in_2 ? and_4_out : 1'bz;  // Controlled_Buffer controlled_buffer_4
  and and_5 (and_5_out, in_1[4], in_2);
  assign out_3[4] = in_2 ? and_5_out : 1'bz;  // Controlled_Buffer controlled_buffer_5
  and and_6 (and_6_out, in_1[5], in_2);
  assign out_3[5] = in_2 ? and_6_out : 1'bz;  // Controlled_Buffer controlled_buffer_6
  and and_7 (and_7_out, in_1[6], in_2);
  assign out_3[6] = in_2 ? and_7_out : 1'bz;  // Controlled_Buffer controlled_buffer_7
  and and_8 (and_8_out, in_1[7], in_2);
  assign out_3[7] = in_2 ? and_8_out : 1'bz;  // Controlled_Buffer controlled_buffer_8
  and and_9 (and_9_out, in_1[8], in_2);
  assign out_3[8] = in_2 ? and_9_out : 1'bz;  // Controlled_Buffer controlled_buffer_9
  and and_10 (and_10_out, in_1[9], in_2);
  assign out_3[9] = in_2 ? and_10_out : 1'bz;  // Controlled_Buffer controlled_buffer_10
  and and_11 (and_11_out, in_1[10], in_2);
  assign out_3[10] = in_2 ? and_11_out : 1'bz;  // Controlled_Buffer controlled_buffer_11
  and and_12 (and_12_out, in_1[11], in_2);
  assign out_3[11] = in_2 ? and_12_out : 1'bz;  // Controlled_Buffer controlled_buffer_12
  and and_13 (and_13_out, in_1[12], in_2);
  assign out_3[12] = in_2 ? and_13_out : 1'bz;  // Controlled_Buffer controlled_buffer_13
  and and_14 (and_14_out, in_1[13], in_2);
  assign out_3[13] = in_2 ? and_14_out : 1'bz;  // Controlled_Buffer controlled_buffer_14
  and and_15 (and_15_out, in_1[14], in_2);
  assign out_3[14] = in_2 ? and_15_out : 1'bz;  // Controlled_Buffer controlled_buffer_15
  and and_16 (and_16_out, in_1[15], in_2);
  assign out_3[15] = in_2 ? and_16_out : 1'bz;  // Controlled_Buffer controlled_buffer_16
endmodule

module CPU_ALU (
  input  [15:0] a,
  input  [15:0] b,
  input  carry_in_d14b9ec6,
  input  r,
  input  d,
  input  in_6,
  input  in_7,
  input  in_8,
  output a_larger_39a03663,
  output equal,
  output zero,
  output [15:0] c,
  output carry_out_c1e17e93,
  output mc
);

  wire adder_1_cout, and_1_out, and_2_out, and_3_out, and_4_out, cpu_adder_8_1_carry_out_c1e17e93,
       cpu_alu_decoder_1_l, cpu_alu_decoder_1_out_3, cpu_alu_decoder_1_out_4, cpu_alu_decoder_1_out_5,
       cpu_alu_decoder_1_out_6, cpu_alu_decoder_1_out_7, cpu_alu_decoder_1_out_8, cpu_alu_decoder_1_out_9,
       cpu_alu_decoder_1_out_10, cpu_alu_decoder_1_out_11, cpu_alu_decoder_1_out_12,
       cpu_alu_decoder_1_out_13, cpu_alu_decoder_1_out_14, cpu_alu_decoder_1_out_15,
       cpu_alu_decoder_1_out_16, cpu_shift_1_carry, or_1_out, or_2_out, subtractor_1_bout;
  wire [15:0] adder_1_out, adder_2_out, cpu_adder_8_1_out_5, cpu_and_1_o, cpu_and_2_o, cpu_not_1_out_2,
       cpu_or_1_l_0_5c1f849d, cpu_shift_1_op, cpu_xor_le_16_1_out_3, divider_1_out, multiplier_1_out,
       subtractor_1_out, subtractor_2_out;

  CPU_AND cpu_and_1 (.a({16{1'b0}}), .b(a), .o(cpu_and_1_o));
  Subtractor #(.width(16)) subtractor_1 (
    .a(b), .b(a), .out(subtractor_1_out), .bin(carry_in_d14b9ec6), .bout(subtractor_1_bout));
  Adder #(.width(16)) adder_1 (.a(b), .b(a), .out(adder_1_out), .cin(carry_in_d14b9ec6), .cout(adder_1_cout));
  Divider #(.width(16)) divider_1 (.a(a), .b(b), .out(divider_1_out));  // open: upper, rem
  Multiplier #(.width(16)) multiplier_1 (.a(a), .b(b), .out(multiplier_1_out));  // open: cin, cout
  Subtractor #(.width(16)) subtractor_2 (.a(a), .b(16'h1), .out(subtractor_2_out));  // open: bin, bout
  Adder #(.width(16)) adder_2 (.a(a), .b(16'h1), .out(adder_2_out));  // open: cin, cout
  CPU_XOR_LE_16 cpu_xor_le_16_1 (
    .b(b), .a(a), .larger(a_larger_39a03663), .equal(equal), .out_3(cpu_xor_le_16_1_out_3));
  CPU_OR cpu_or_1 (.a(a), .b(b), .L_0_5c1f849d(cpu_or_1_l_0_5c1f849d));
  CPU_AND cpu_and_2 (.a(a), .b(b), .o(cpu_and_2_o));
  CPU_NOT cpu_not_1 (.i(a), .out_2(cpu_not_1_out_2));
  CPU_ADDER_8 cpu_adder_8_1 (
    .a(a), .b(b), .carry_in_d14b9ec6(carry_in_d14b9ec6), .out_5(cpu_adder_8_1_out_5),
    .carry_out_c1e17e93(cpu_adder_8_1_carry_out_c1e17e93));
  CPU_SHIFT cpu_shift_1 (
    .carry_in_d14b9ec6(carry_in_d14b9ec6), .i(b), .LRcount(a), .R(cpu_alu_decoder_1_out_3),
    .L(cpu_alu_decoder_1_out_4), .op(cpu_shift_1_op), .carry(cpu_shift_1_carry));  // open: out_6
  CPU_ALU_DECODER cpu_alu_decoder_1 (
    .in_1({d, in_6, in_7, in_8}), .out_13(cpu_alu_decoder_1_out_13), .out_14(cpu_alu_decoder_1_out_14),
    .out_15(cpu_alu_decoder_1_out_15), .out_16(cpu_alu_decoder_1_out_16), .M(mc), .L(cpu_alu_decoder_1_l),
    .out_3(cpu_alu_decoder_1_out_3), .out_4(cpu_alu_decoder_1_out_4), .out_5(cpu_alu_decoder_1_out_5),
    .out_6(cpu_alu_decoder_1_out_6), .out_7(cpu_alu_decoder_1_out_7), .out_8(cpu_alu_decoder_1_out_8),
    .out_9(cpu_alu_decoder_1_out_9), .out_10(cpu_alu_decoder_1_out_10), .out_11(cpu_alu_decoder_1_out_11),
    .out_12(cpu_alu_decoder_1_out_12));
  or or_1 (or_1_out, cpu_alu_decoder_1_out_4, cpu_alu_decoder_1_out_3);
  CPU_E cpu_e_1 (.in_1(cpu_and_1_o), .in_2(cpu_alu_decoder_1_out_16), .out_3(c));
  CPU_E cpu_e_2 (.in_1(subtractor_1_out), .in_2(cpu_alu_decoder_1_out_15), .out_3(c));
  CPU_E cpu_e_3 (.in_1(adder_1_out), .in_2(cpu_alu_decoder_1_out_14), .out_3(c));
  CPU_E cpu_e_4 (.in_1(divider_1_out), .in_2(cpu_alu_decoder_1_out_13), .out_3(c));
  CPU_E cpu_e_5 (.in_1(multiplier_1_out), .in_2(cpu_alu_decoder_1_out_12), .out_3(c));
  CPU_E cpu_e_6 (.in_1(subtractor_2_out), .in_2(cpu_alu_decoder_1_out_11), .out_3(c));
  CPU_E cpu_e_7 (.in_1(adder_2_out), .in_2(cpu_alu_decoder_1_out_10), .out_3(c));
  CPU_E cpu_e_8 (.in_1(cpu_xor_le_16_1_out_3), .in_2(cpu_alu_decoder_1_out_8), .out_3(c));
  CPU_E cpu_e_9 (.in_1(cpu_or_1_l_0_5c1f849d), .in_2(or_2_out), .out_3(c));
  or or_2 (or_2_out, cpu_alu_decoder_1_out_9, cpu_alu_decoder_1_out_7);
  CPU_E cpu_e_10 (.in_1(cpu_and_2_o), .in_2(cpu_alu_decoder_1_out_6), .out_3(c));
  CPU_E cpu_e_11 (.in_1(cpu_not_1_out_2), .in_2(cpu_alu_decoder_1_out_5), .out_3(c));
  CPU_E cpu_e_12 (.in_1(cpu_shift_1_op), .in_2(or_1_out), .out_3(c));
  CPU_E cpu_e_13 (.in_1(cpu_adder_8_1_out_5), .in_2(cpu_alu_decoder_1_l), .out_3(c));
  and and_1 (and_1_out, subtractor_1_bout, cpu_alu_decoder_1_out_15);
  assign carry_out_c1e17e93 = cpu_alu_decoder_1_out_15 ? and_1_out : 1'bz;  // Controlled_Buffer controlled_buffer_1
  and and_2 (and_2_out, cpu_alu_decoder_1_out_14, adder_1_cout);
  assign carry_out_c1e17e93 = cpu_alu_decoder_1_out_14 ? and_2_out : 1'bz;  // Controlled_Buffer controlled_buffer_2
  and and_3 (and_3_out, cpu_shift_1_carry, or_1_out);
  assign carry_out_c1e17e93 = or_1_out ? and_3_out : 1'bz;  // Controlled_Buffer controlled_buffer_3
  and and_4 (and_4_out, cpu_adder_8_1_carry_out_c1e17e93, cpu_alu_decoder_1_l);
  assign carry_out_c1e17e93 = cpu_alu_decoder_1_l ? and_4_out : 1'bz;  // Controlled_Buffer controlled_buffer_4
  CPU_Z cpu_z_1 (.i(c), .o(zero));

  // Notes on the sheet:
  //   dec
  //   inc
endmodule

module CPU_BUS_1 (
  input  [15:0] i,
  input  bus_1_0423081d,
  output [15:0] o
);

  wire not_1_out;

  and and_1 (o[15], i[15], not_1_out);
  and and_2 (o[14], i[14], not_1_out);
  and and_3 (o[13], i[13], not_1_out);
  and and_4 (o[12], i[12], not_1_out);
  and and_5 (o[11], i[11], not_1_out);
  and and_6 (o[10], i[10], not_1_out);
  and and_7 (o[9], i[9], not_1_out);
  and and_8 (o[8], i[8], not_1_out);
  and and_9 (o[7], i[7], not_1_out);
  and and_10 (o[6], i[6], not_1_out);
  and and_11 (o[5], i[5], not_1_out);
  and and_12 (o[4], i[4], not_1_out);
  and and_13 (o[3], i[3], not_1_out);
  and and_14 (o[2], i[2], not_1_out);
  and and_15 (o[1], i[1], not_1_out);
  or or_1 (o[0], i[0], bus_1_0423081d);
  not not_1 (not_1_out, bus_1_0423081d);
endmodule

module CPU_ACCUMULATOR (
  input  [15:0] i,
  input  r,
  input  s,
  input  e,
  output [15:0] ACC,
  output [15:0] o
);

  CPU_REGISTER_16 cpu_register_16_1 (.i(i), .r(r), .s(s), .e(e), .REG(ACC), .L_0_5c1f849d(o));
endmodule

module CPU_R (
  input  [15:0] i,
  input  r,
  input  s,
  input  e,
  output [15:0] \reg ,
  output [15:0] o
);

  CPU_REGISTER_16 cpu_register_16_1 (.i(i), .r(r), .s(s), .e(e), .REG(\reg ), .L_0_5c1f849d(o));
endmodule

module CPU_TMP (
  input  [15:0] i,
  input  r,
  input  s,
  output [15:0] o
);

  wire [15:0] controlled_buffer_1_out;

  assign controlled_buffer_1_out = s ? i : 16'bz;  // Controlled_Buffer controlled_buffer_1
  CPU_MEM_16 cpu_mem_16_1 (.in_1(controlled_buffer_1_out), .r(r), .s(s), .out_4(o));
endmodule

module CPU_STEPPER (
  input  clks,
  input  reset,
  input  st,
  input  clk,
  output f_e,
  output [7:0] execute,
  output step_1_a10c3af4,
  output out_8,
  output out_9,
  output step_2_8c45f034,
  output step_3_71bf9378,
  output step_4_8482adae,
  output step_5_9168e5f1,
  output step_6_40d4d5bc,
  output step_7_b995d97f,
  output step_8_8b8c5577,
  output step_9_25733d10,
  output step_10_d1921302,
  output step_11_2c52167f,
  output step_12_1f4f3d86,
  output step_13_cd0165a2,
  output step_14_c27f319a,
  output step_15_f0b56f10,
  output step_17_1b97b40f,
  output step_18_37d11f24
);

  wire cpu_step_mem_1_out_3, cpu_step_mem_2_out_3, cpu_step_mem_3_out_3, cpu_step_mem_4_out_3,
       cpu_step_mem_5_out_3, cpu_step_mem_6_out_3, cpu_step_mem_7_out_3, cpu_step_mem_8_out_3,
       cpu_step_mem_9_out_3, cpu_step_mem_10_out_3, cpu_step_mem_11_out_3, cpu_step_mem_12_out_3,
       cpu_step_mem_13_out_3, cpu_step_mem_14_out_3, cpu_step_mem_15_out_3, cpu_step_mem_16_out_3,
       cpu_step_mem_17_out_3, cpu_step_mem_18_out_3, cpu_step_mem_19_out_3, cpu_step_mem_20_out_3,
       cpu_step_mem_21_out_3, cpu_step_mem_22_out_3, cpu_step_mem_23_out_3, cpu_step_mem_24_out_3,
       cpu_step_mem_25_out_3, cpu_step_mem_26_out_3, cpu_step_mem_27_out_3, cpu_step_mem_28_out_3,
       cpu_step_mem_29_out_3, cpu_step_mem_30_out_3, cpu_step_mem_31_out_3, cpu_step_mem_32_out_3,
       cpu_step_mem_33_out_3, cpu_step_mem_34_out_3, cpu_step_mem_35_out_3, cpu_step_mem_36_out_3,
       cpu_step_mem_37_out_3, cpu_step_mem_38_out_3, nor_1_out, not_1_out, not_2_out, not_3_out, not_4_out,
       not_5_out, not_6_out, not_7_out, not_8_out, not_9_out, not_10_out, not_11_out, not_12_out, not_13_out,
       not_14_out, not_15_out, not_16_out, not_17_out, not_18_out, not_19_out, not_20_out, not_21_out,
       or_1_out, or_2_out, or_3_out;

  or or_1 (or_1_out, reset, st, cpu_step_mem_38_out_3);
  not not_1 (not_1_out, clk);
  Counter #(.max('hf), .trigger("falling"), .width(4)) counter_1 (
    .load(1'b0), .count(1'b1), .Q(execute[3:0]), .up(1'b1), .clk(clk), .clr(step_3_71bf9378));  // open: D, carry
  not not_2 (not_2_out, or_1_out);
  or or_2 (or_2_out, or_1_out, clk);
  or or_3 (or_3_out, or_1_out, not_1_out);
  or or_4 (out_9, or_1_out, not_3_out);
  CPU_STEP_MEM cpu_step_mem_1 (.in_1(not_2_out), .in_2(or_2_out), .out_3(cpu_step_mem_1_out_3));
  not not_3 (not_3_out, cpu_step_mem_2_out_3);
  CPU_STEP_MEM cpu_step_mem_2 (.in_1(cpu_step_mem_1_out_3), .in_2(or_3_out), .out_3(cpu_step_mem_2_out_3));
  and and_1 (step_2_8c45f034, cpu_step_mem_2_out_3, not_4_out);
  nor nor_1 (nor_1_out, out_9, step_2_8c45f034, step_3_71bf9378);
  not not_4 (not_4_out, cpu_step_mem_4_out_3);
  CPU_STEP_MEM cpu_step_mem_3 (.in_1(cpu_step_mem_2_out_3), .in_2(or_2_out), .out_3(cpu_step_mem_3_out_3));
  CPU_MEM_1 cpu_mem_1_1 (.in_1(nor_1_out), .in_2(clks), .r(reset), .out_4(f_e));
  CPU_STEP_MEM cpu_step_mem_4 (.in_1(cpu_step_mem_3_out_3), .in_2(or_3_out), .out_3(cpu_step_mem_4_out_3));
  and and_2 (step_3_71bf9378, cpu_step_mem_4_out_3, not_5_out);
  CPU_STEP_MEM cpu_step_mem_5 (.in_1(cpu_step_mem_4_out_3), .in_2(or_2_out), .out_3(cpu_step_mem_5_out_3));
  not not_5 (not_5_out, cpu_step_mem_6_out_3);
  CPU_STEP_MEM cpu_step_mem_6 (.in_1(cpu_step_mem_5_out_3), .in_2(or_3_out), .out_3(cpu_step_mem_6_out_3));
  and and_3 (step_4_8482adae, cpu_step_mem_6_out_3, not_6_out);
  not not_6 (not_6_out, cpu_step_mem_8_out_3);
  CPU_STEP_MEM cpu_step_mem_7 (.in_1(cpu_step_mem_6_out_3), .in_2(or_2_out), .out_3(cpu_step_mem_7_out_3));
  and and_4 (step_5_9168e5f1, cpu_step_mem_8_out_3, not_7_out);
  CPU_STEP_MEM cpu_step_mem_8 (.in_1(cpu_step_mem_7_out_3), .in_2(or_3_out), .out_3(cpu_step_mem_8_out_3));
  not not_7 (not_7_out, cpu_step_mem_10_out_3);
  CPU_STEP_MEM cpu_step_mem_9 (.in_1(cpu_step_mem_8_out_3), .in_2(or_2_out), .out_3(cpu_step_mem_9_out_3));
  CPU_STEP_MEM cpu_step_mem_10 (.in_1(cpu_step_mem_9_out_3), .in_2(or_3_out), .out_3(cpu_step_mem_10_out_3));
  and and_5 (step_6_40d4d5bc, cpu_step_mem_10_out_3, not_8_out);
  CPU_STEP_MEM cpu_step_mem_11 (.in_1(cpu_step_mem_10_out_3), .in_2(or_2_out), .out_3(cpu_step_mem_11_out_3));
  not not_8 (not_8_out, cpu_step_mem_12_out_3);
  CPU_STEP_MEM cpu_step_mem_12 (.in_1(cpu_step_mem_11_out_3), .in_2(or_3_out), .out_3(cpu_step_mem_12_out_3));
  and and_6 (step_7_b995d97f, cpu_step_mem_12_out_3, not_9_out);
  not not_9 (not_9_out, cpu_step_mem_14_out_3);
  CPU_STEP_MEM cpu_step_mem_13 (.in_1(cpu_step_mem_12_out_3), .in_2(or_2_out), .out_3(cpu_step_mem_13_out_3));
  CPU_STEP_MEM cpu_step_mem_14 (.in_1(cpu_step_mem_13_out_3), .in_2(or_3_out), .out_3(cpu_step_mem_14_out_3));
  and and_7 (step_8_8b8c5577, cpu_step_mem_14_out_3, not_10_out);
  CPU_STEP_MEM cpu_step_mem_15 (.in_1(cpu_step_mem_14_out_3), .in_2(or_2_out), .out_3(cpu_step_mem_15_out_3));
  not not_10 (not_10_out, cpu_step_mem_16_out_3);
  CPU_STEP_MEM cpu_step_mem_16 (.in_1(cpu_step_mem_15_out_3), .in_2(or_3_out), .out_3(cpu_step_mem_16_out_3));
  and and_8 (step_9_25733d10, cpu_step_mem_16_out_3, not_11_out);
  not not_11 (not_11_out, cpu_step_mem_18_out_3);
  CPU_STEP_MEM cpu_step_mem_17 (.in_1(cpu_step_mem_16_out_3), .in_2(or_2_out), .out_3(cpu_step_mem_17_out_3));
  and and_9 (step_10_d1921302, cpu_step_mem_18_out_3, not_12_out);
  CPU_STEP_MEM cpu_step_mem_18 (.in_1(cpu_step_mem_17_out_3), .in_2(or_3_out), .out_3(cpu_step_mem_18_out_3));
  not not_12 (not_12_out, cpu_step_mem_20_out_3);
  CPU_STEP_MEM cpu_step_mem_19 (.in_1(cpu_step_mem_18_out_3), .in_2(or_2_out), .out_3(cpu_step_mem_19_out_3));
  CPU_STEP_MEM cpu_step_mem_20 (.in_1(cpu_step_mem_19_out_3), .in_2(or_3_out), .out_3(cpu_step_mem_20_out_3));
  and and_10 (step_11_2c52167f, cpu_step_mem_20_out_3, not_13_out);
  CPU_STEP_MEM cpu_step_mem_21 (.in_1(cpu_step_mem_20_out_3), .in_2(or_2_out), .out_3(cpu_step_mem_21_out_3));
  not not_13 (not_13_out, cpu_step_mem_22_out_3);
  CPU_STEP_MEM cpu_step_mem_22 (.in_1(cpu_step_mem_21_out_3), .in_2(or_3_out), .out_3(cpu_step_mem_22_out_3));
  and and_11 (step_12_1f4f3d86, cpu_step_mem_22_out_3, not_14_out);
  CPU_STEP_MEM cpu_step_mem_23 (.in_1(cpu_step_mem_22_out_3), .in_2(or_2_out), .out_3(cpu_step_mem_23_out_3));
  not not_14 (not_14_out, cpu_step_mem_24_out_3);
  CPU_STEP_MEM cpu_step_mem_24 (.in_1(cpu_step_mem_23_out_3), .in_2(or_3_out), .out_3(cpu_step_mem_24_out_3));
  and and_12 (step_13_cd0165a2, cpu_step_mem_24_out_3, not_15_out);
  CPU_STEP_MEM cpu_step_mem_25 (.in_1(cpu_step_mem_24_out_3), .in_2(or_2_out), .out_3(cpu_step_mem_25_out_3));
  not not_15 (not_15_out, cpu_step_mem_26_out_3);
  CPU_STEP_MEM cpu_step_mem_26 (.in_1(cpu_step_mem_25_out_3), .in_2(or_3_out), .out_3(cpu_step_mem_26_out_3));
  and and_13 (step_14_c27f319a, cpu_step_mem_26_out_3, not_16_out);
  not not_16 (not_16_out, cpu_step_mem_28_out_3);
  CPU_STEP_MEM cpu_step_mem_27 (.in_1(cpu_step_mem_26_out_3), .in_2(or_2_out), .out_3(cpu_step_mem_27_out_3));
  and and_14 (step_15_f0b56f10, cpu_step_mem_28_out_3, not_17_out);
  CPU_STEP_MEM cpu_step_mem_28 (.in_1(cpu_step_mem_27_out_3), .in_2(or_3_out), .out_3(cpu_step_mem_28_out_3));
  CPU_STEP_MEM cpu_step_mem_29 (.in_1(cpu_step_mem_28_out_3), .in_2(or_2_out), .out_3(cpu_step_mem_29_out_3));
  not not_17 (not_17_out, cpu_step_mem_30_out_3);
  CPU_STEP_MEM cpu_step_mem_30 (.in_1(cpu_step_mem_29_out_3), .in_2(or_3_out), .out_3(cpu_step_mem_30_out_3));
  and and_15 (step_1_a10c3af4, cpu_step_mem_30_out_3, not_18_out);
  not not_18 (not_18_out, cpu_step_mem_32_out_3);
  CPU_STEP_MEM cpu_step_mem_31 (.in_1(cpu_step_mem_30_out_3), .in_2(or_2_out), .out_3(cpu_step_mem_31_out_3));
  CPU_STEP_MEM cpu_step_mem_32 (.in_1(cpu_step_mem_31_out_3), .in_2(or_3_out), .out_3(cpu_step_mem_32_out_3));
  and and_16 (step_17_1b97b40f, cpu_step_mem_32_out_3, not_19_out);
  not not_19 (not_19_out, cpu_step_mem_34_out_3);
  CPU_STEP_MEM cpu_step_mem_33 (.in_1(cpu_step_mem_32_out_3), .in_2(or_2_out), .out_3(cpu_step_mem_33_out_3));
  and and_17 (step_18_37d11f24, cpu_step_mem_34_out_3, not_20_out);
  CPU_STEP_MEM cpu_step_mem_34 (.in_1(cpu_step_mem_33_out_3), .in_2(or_3_out), .out_3(cpu_step_mem_34_out_3));
  CPU_STEP_MEM cpu_step_mem_35 (.in_1(cpu_step_mem_34_out_3), .in_2(or_2_out), .out_3(cpu_step_mem_35_out_3));
  not not_20 (not_20_out, cpu_step_mem_36_out_3);
  CPU_STEP_MEM cpu_step_mem_36 (.in_1(cpu_step_mem_35_out_3), .in_2(or_3_out), .out_3(cpu_step_mem_36_out_3));
  and and_18 (out_8, cpu_step_mem_36_out_3, not_21_out);
  not not_21 (not_21_out, cpu_step_mem_38_out_3);
  CPU_STEP_MEM cpu_step_mem_37 (.in_1(cpu_step_mem_36_out_3), .in_2(or_2_out), .out_3(cpu_step_mem_37_out_3));
  CPU_STEP_MEM cpu_step_mem_38 (.in_1(cpu_step_mem_37_out_3), .in_2(or_3_out), .out_3(cpu_step_mem_38_out_3));

  assign execute[7:4] = 4'b0000;
endmodule

module CPU (
  input  clock,
  input  r,
  input  [15:0] DATA_BUS_IN,
  input  W,
  output [15:0] R0,
  output [15:0] R1,
  output [15:0] R2,
  output [15:0] R3,
  output [15:0] R4,
  output [15:0] R5,
  output [15:0] R6_TMP,
  output [15:0] SP,
  output [15:0] INDEX,
  output [15:0] FU,
  output clkl,
  output clke,
  output clks,
  output mc,
  output END,
  output [1:0] CNTRL_BUS,
  output [15:0] out_21,
  output [15:0] out_22,
  output [15:0] ADDR_BUS,
  output [4:0] FLAGS,
  output [15:0] DATA_BUS_OUT
);

  wire and_1_out, B, C, cpu_alu_1_a_larger_39a03663, cpu_alu_1_carry_out_c1e17e93, cpu_alu_1_equal,
       cpu_alu_1_zero, cpu_carry_temp_1_o, cpu_control_section_5ba48747_1_acc_e,
       cpu_control_section_5ba48747_1_acc_s, cpu_control_section_5ba48747_1_alu_0,
       cpu_control_section_5ba48747_1_alu_1, cpu_control_section_5ba48747_1_alu_2,
       cpu_control_section_5ba48747_1_alu_3, cpu_control_section_5ba48747_1_flag_e,
       cpu_control_section_5ba48747_1_flags_s, cpu_control_section_5ba48747_1_iar_e,
       cpu_control_section_5ba48747_1_iar_s, cpu_control_section_5ba48747_1_ir_e,
       cpu_control_section_5ba48747_1_ir_s, fue, fus, lre, lrs, MARS, not_1_out, r1e, r1s, r2e, r2s, r3e,
       r3s, r4e, r4s, r5e, r5s, r6tmpe, r6tmps, roe, ros, sp_e, sp_s, TS;
  wire [15:0] cpu_accumulator_1_acc, cpu_alu_1_c, cpu_bus_1_1_o, cpu_tmp_1_o;

  // Probe on cpu_accumulator_1_acc
  CPU_ACCUMULATOR cpu_accumulator_1 (
    .i(cpu_alu_1_c), .r(r), .s(cpu_control_section_5ba48747_1_acc_s),
    .e(cpu_control_section_5ba48747_1_acc_e), .ACC(cpu_accumulator_1_acc), .o(DATA_BUS_IN));
  CPU_TMP cpu_tmp_1 (.i(DATA_BUS_IN), .r(r), .s(TS), .o(cpu_tmp_1_o));
  CPU_BUS_1 cpu_bus_1_1 (.bus_1_0423081d(B), .i(cpu_tmp_1_o), .o(cpu_bus_1_1_o));
  CPU_ALU cpu_alu_1 (
    .r(r), .a(DATA_BUS_IN), .b(cpu_bus_1_1_o), .carry_in_d14b9ec6(FLAGS[4]),
    .d(cpu_control_section_5ba48747_1_alu_3), .in_6(cpu_control_section_5ba48747_1_alu_2),
    .in_7(cpu_control_section_5ba48747_1_alu_1), .in_8(cpu_control_section_5ba48747_1_alu_0),
    .c(cpu_alu_1_c), .carry_out_c1e17e93(cpu_alu_1_carry_out_c1e17e93),
    .a_larger_39a03663(cpu_alu_1_a_larger_39a03663), .equal(cpu_alu_1_equal), .zero(cpu_alu_1_zero), .mc(mc));
  CPU_R cpu_r_1 (.i(DATA_BUS_IN), .r(r), .s(ros), .e(roe), .\reg (R0), .o(DATA_BUS_IN));
  not not_1 (not_1_out, END);
  and and_1 (and_1_out, not_1_out, clock);
  and and_2 (FLAGS[4], C, cpu_carry_temp_1_o);
  CPU_CLK cpu_clk_1 (.clkin(and_1_out), .clk(clkl), .clks(clks), .clke(clke));
  CPU_CARRY_TEMP cpu_carry_temp_1 (.c(FLAGS[3]), .r(r), .s(TS), .o(cpu_carry_temp_1_o));
  CPU_R cpu_r_2 (.i(DATA_BUS_IN), .r(r), .s(r1s), .e(r1e), .\reg (R1), .o(DATA_BUS_IN));
  CPU_FLAGS cpu_flags_1 (
    .C(cpu_alu_1_carry_out_c1e17e93), .A(cpu_alu_1_a_larger_39a03663), .E(cpu_alu_1_equal),
    .Z(cpu_alu_1_zero), .r(r), .s(cpu_control_section_5ba48747_1_flags_s),
    .in_7(cpu_control_section_5ba48747_1_flag_e), .out_8(FLAGS[3]), .out_9(FLAGS[2]), .out_10(FLAGS[1]),
    .out_11(FLAGS[0]), .op(DATA_BUS_IN));
  CPU_R cpu_r_3 (.i(DATA_BUS_IN), .r(r), .s(r2s), .e(r2e), .\reg (R2), .o(DATA_BUS_IN));
  CPU_CONTROL_SECTION_5ba48747 cpu_control_section_5ba48747_1 (
    .clks(clks), .clke(clke), .in_5(FLAGS[3]), .A(FLAGS[2]), .E(FLAGS[1]), .Z(FLAGS[0]), .r(r), .clk(clkl),
    .IR_IN_687096ad(out_21), .R3_E(r3e), .R2_E(r2e), .R1_E(r1e), .R0_E(roe),
    .ALU_2(cpu_control_section_5ba48747_1_alu_2), .ALU_3(cpu_control_section_5ba48747_1_alu_3),
    .BUS_1_2bb40982(B), .ACC_E(cpu_control_section_5ba48747_1_acc_e),
    .IR_E(cpu_control_section_5ba48747_1_ir_e), .IAR_E(cpu_control_section_5ba48747_1_iar_e),
    .CNTRL_E(CNTRL_BUS[0]), .R6_TMP_E(r6tmpe), .FLAG_E(cpu_control_section_5ba48747_1_flag_e),
    .STACK_E(sp_e), .INDEX_E(lre), .FPU_E(fue), .R5_E(r5e), .R4_E(r4e), .END(END), .R3_S(r3s), .R2_S(r2s),
    .R1_S(r1s), .R0_S(ros), .ALU_1(cpu_control_section_5ba48747_1_alu_1),
    .ALU_0(cpu_control_section_5ba48747_1_alu_0), .C(C), .MAR_S(MARS),
    .ACC_S(cpu_control_section_5ba48747_1_acc_s), .IR_S(cpu_control_section_5ba48747_1_ir_s),
    .IAR_S(cpu_control_section_5ba48747_1_iar_s), .CNTRL_S(CNTRL_BUS[1]), .TMP_S(TS), .R6_TMP_S(r6tmps),
    .FLAGS_S(cpu_control_section_5ba48747_1_flags_s), .STACK_S(sp_s), .INDEX_S(lrs), .FPU_S(fus), .R5_S(r5s),
    .R4_S(r4s));
  CPU_R cpu_r_4 (.i(DATA_BUS_IN), .r(r), .s(r3s), .e(r3e), .\reg (R3), .o(DATA_BUS_IN));
  CPU_R cpu_r_5 (.i(DATA_BUS_IN), .r(r), .s(r4s), .e(r4e), .\reg (R4), .o(DATA_BUS_IN));
  CPU_R cpu_r_6 (.i(DATA_BUS_IN), .r(r), .s(r5s), .e(r5e), .\reg (R5), .o(DATA_BUS_IN));
  CPU_IAR cpu_iar_1 (
    .i(DATA_BUS_IN), .W(W), .r(r), .s(cpu_control_section_5ba48747_1_iar_s),
    .e(cpu_control_section_5ba48747_1_iar_e), .IAR(out_22), .o(DATA_BUS_IN));
  CPU_R cpu_r_7 (.i(DATA_BUS_IN), .r(r), .s(r6tmps), .e(r6tmpe), .\reg (R6_TMP), .o(DATA_BUS_IN));
  CPU_IR cpu_ir_1 (
    .r(r), .i(DATA_BUS_IN), .s(cpu_control_section_5ba48747_1_ir_s), .e(cpu_control_section_5ba48747_1_ir_e),
    .o(out_21), .en_o(DATA_BUS_IN));
  CPU_R cpu_r_8 (.i(DATA_BUS_IN), .r(r), .s(sp_s), .e(sp_e), .\reg (SP), .o(DATA_BUS_IN));
  CPU_REGISTER_16 cpu_register_16_1 (.i(DATA_BUS_IN), .r(r), .s(MARS), .e(1'b1), .L_0_5c1f849d(ADDR_BUS));  // open: REG
  CPU_R cpu_r_9 (.i(DATA_BUS_IN), .r(r), .s(lrs), .e(lre), .\reg (INDEX), .o(DATA_BUS_IN));
  CPU_R cpu_r_10 (.i(DATA_BUS_IN), .r(r), .s(fus), .e(fue), .\reg (FU), .o(DATA_BUS_IN));

  assign DATA_BUS_OUT = DATA_BUS_IN;
endmodule

module CPU_IAR (
  input  [15:0] i,
  input  r,
  input  W,
  input  s,
  input  e,
  output [15:0] IAR,
  output [15:0] o
);

  wire not_1_out;
  wire [15:0] controlled_buffer_1_out;

  assign controlled_buffer_1_out = not_1_out ? i : 16'bz;  // Controlled_Buffer controlled_buffer_1
  not not_1 (not_1_out, W);
  CPU_REGISTER_16 cpu_register_16_1 (.i(controlled_buffer_1_out), .r(r), .s(s), .e(e), .REG(IAR), .L_0_5c1f849d(o));
endmodule

module CPU_IR (
  input  [15:0] i,
  input  r,
  input  s,
  input  e,
  output [15:0] o,
  output [15:0] en_o
);

  CPU_MEM_16 cpu_mem_16_1 (.in_1(i), .r(r), .s(s), .out_4(o));
  CPU_ENABLE_16 cpu_enable_16_1 (.in_1(o), .in_2(e), .out_3(en_o));
endmodule

module CPU_FLAGS (
  input  C,
  input  A,
  input  E,
  input  Z,
  input  r,
  input  s,
  input  in_7,
  output out_8,
  output out_9,
  output out_10,
  output out_11,
  output [15:0] op
);

  CPU_MEM_1 cpu_mem_1_1 (.in_1(C), .in_2(s), .r(r), .out_4(out_8));
  CPU_MEM_1 cpu_mem_1_2 (.in_1(A), .in_2(s), .r(r), .out_4(out_9));
  CPU_MEM_1 cpu_mem_1_3 (.in_1(E), .in_2(s), .r(r), .out_4(out_10));
  CPU_MEM_1 cpu_mem_1_4 (.in_1(Z), .in_2(s), .r(r), .out_4(out_11));
  CPU_ENABLE_16 cpu_enable_16_1 (.in_1({{12{1'b0}}, out_11, out_10, out_9, out_8}), .in_2(in_7), .out_3(op));
endmodule

module CPU_CONTROL_SECTION_5ba48747 (
  input  clks,
  input  clke,
  input  r,
  input  clk,
  input  in_5,
  input  A,
  input  E,
  input  Z,
  input  [15:0] IR_IN_687096ad,
  output ALU_2,
  output ALU_1,
  output ALU_3,
  output ALU_0,
  output C,
  output BUS_1_2bb40982,
  output MAR_S,
  output ACC_S,
  output ACC_E,
  output IR_S,
  output IR_E,
  output IAR_S,
  output IAR_E,
  output CNTRL_S,
  output CNTRL_E,
  output TMP_S,
  output R6_TMP_E,
  output R6_TMP_S,
  output FLAGS_S,
  output FLAG_E,
  output STACK_S,
  output STACK_E,
  output INDEX_S,
  output INDEX_E,
  output FPU_S,
  output FPU_E,
  output R5_E,
  output R5_S,
  output R4_E,
  output R4_S,
  output R3_E,
  output R3_S,
  output R2_E,
  output R2_S,
  output R1_E,
  output R1_S,
  output R0_E,
  output R0_S,
  output END
);

  wire Ae, and_18_out, As, Be, Bs, cpu_4x16_control_1_ch, cpu_stepper_1_out_9, cpu_stepper_1_step_2_8c45f034,
       cpu_stepper_1_step_3_71bf9378, cpu_ucode_rom_1_out_8, cpu_ucode_rom_1_out_9, cpu_ucode_rom_1_out_10,
       cpu_ucode_rom_1_out_11, cpu_ucode_rom_1_out_12, cpu_ucode_rom_1_out_13, cpu_ucode_rom_1_out_14,
       cpu_ucode_rom_1_out_15, cpu_ucode_rom_1_out_16, cpu_ucode_rom_1_out_17, cpu_ucode_rom_1_out_23,
       cpu_ucode_rom_1_out_24, cpu_ucode_rom_1_out_25, cpu_ucode_rom_1_out_26, cpu_ucode_rom_1_out_27,
       cpu_ucode_rom_1_out_28, cpu_ucode_rom_1_out_29, cpu_ucode_rom_1_out_30, cpu_ucode_rom_1_out_31,
       cpu_ucode_rom_1_out_32, cpu_ucode_rom_1_out_33, f_e, JI, L_3_11582392, not_1_out, not_2_out,
       not_3_out, or_1_out, or_2_out, or_3_out, or_4_out, or_5_out, or_6_out, or_7_out, or_8_out, or_9_out,
       or_10_out, or_11_out, or_12_out, or_13_out, or_14_out, or_15_out, or_16_out, or_17_out, or_18_out,
       or_19_out, STOP;
  wire [7:0] execute;
  wire [15:0] cpu_ucode_decoder_1_op, cpu_ucode_decoder_2_op, RA_RB_E, RA_RB_S;

  and and_1 (BUS_1_2bb40982, or_1_out, clke);
  and and_2 (ACC_E, or_2_out, clke);
  and and_3 (IR_E, or_3_out, clke);
  and and_4 (IAR_E, or_4_out, clke);
  and and_5 (CNTRL_E, or_5_out, clke);
  and and_6 (R6_TMP_E, cpu_ucode_rom_1_out_12, clke);
  and and_7 (FLAG_E, or_6_out, clke);
  and and_8 (STACK_E, or_7_out, clke);
  and and_9 (INDEX_E, or_8_out, clke);
  and and_10 (FPU_E, or_9_out, clke);
  and and_11 (R5_E, clke, RA_RB_E[5]);
  and and_12 (R4_E, clke, RA_RB_E[4]);
  and and_13 (R3_E, clke, RA_RB_E[3]);
  and and_14 (R2_E, clke, RA_RB_E[2]);
  and and_15 (R1_E, clke, RA_RB_E[1]);
  and and_16 (R0_E, clke, RA_RB_E[0]);
  or or_1 (or_1_out, cpu_stepper_1_out_9, cpu_ucode_rom_1_out_17);
  or or_2 (or_2_out, cpu_ucode_rom_1_out_16, cpu_stepper_1_step_3_71bf9378, RA_RB_E[14]);
  or or_3 (or_3_out, cpu_ucode_rom_1_out_15, RA_RB_E[13]);
  or or_4 (or_4_out, cpu_stepper_1_out_9, cpu_ucode_rom_1_out_14, RA_RB_E[12]);
  or or_5 (or_5_out, cpu_stepper_1_step_2_8c45f034, cpu_ucode_rom_1_out_13, RA_RB_E[11]);
  or or_6 (or_6_out, cpu_ucode_rom_1_out_11, RA_RB_E[9]);
  or or_7 (or_7_out, cpu_ucode_rom_1_out_10, RA_RB_E[8]);
  or or_8 (or_8_out, cpu_ucode_rom_1_out_9, RA_RB_E[7]);
  or or_9 (or_9_out, cpu_ucode_rom_1_out_8, RA_RB_E[6]);
  CPU_4x16_CONTROL cpu_4x16_control_1 (
    .L_3_11582392(IR_IN_687096ad[7]), .L_2_1ea30b77(IR_IN_687096ad[6]), .L_1_b91444db(IR_IN_687096ad[5]),
    .L_0_5c1f849d(IR_IN_687096ad[4]), .C(in_5), .A(A), .E(E), .Z(Z), .Ch(cpu_4x16_control_1_ch));
  and and_17 (JI, cpu_4x16_control_1_ch, and_18_out, L_3_11582392);
  and and_18 (and_18_out, IR_IN_687096ad[10], IR_IN_687096ad[11], not_1_out, not_2_out, IR_IN_687096ad[14], not_3_out);
  CPU_uCode_ROM cpu_ucode_rom_1 (
    .f_e(f_e), .am0(IR_IN_687096ad[8]), .am1(IR_IN_687096ad[9]), .opcode(IR_IN_687096ad[15:10]),
    .execute(execute), .op(Ae), .out_7(Be), .out_8(cpu_ucode_rom_1_out_8), .out_9(cpu_ucode_rom_1_out_9),
    .out_10(cpu_ucode_rom_1_out_10), .out_11(cpu_ucode_rom_1_out_11), .out_12(cpu_ucode_rom_1_out_12),
    .out_13(cpu_ucode_rom_1_out_13), .out_14(cpu_ucode_rom_1_out_14), .out_15(cpu_ucode_rom_1_out_15),
    .out_16(cpu_ucode_rom_1_out_16), .out_17(cpu_ucode_rom_1_out_17), .out_18(ALU_3), .out_19(ALU_2),
    .out_20(ALU_1), .out_21(ALU_0), .out_22(C), .out_23(cpu_ucode_rom_1_out_23),
    .out_24(cpu_ucode_rom_1_out_24), .out_25(cpu_ucode_rom_1_out_25), .out_26(cpu_ucode_rom_1_out_26),
    .out_27(cpu_ucode_rom_1_out_27), .out_28(cpu_ucode_rom_1_out_28), .out_29(cpu_ucode_rom_1_out_29),
    .out_30(cpu_ucode_rom_1_out_30), .out_31(cpu_ucode_rom_1_out_31), .out_32(cpu_ucode_rom_1_out_32),
    .out_33(cpu_ucode_rom_1_out_33), .out_34(STOP), .out_35(END), .out_36(As), .out_37(Bs));
  not not_1 (not_1_out, IR_IN_687096ad[12]);
  not not_2 (not_2_out, IR_IN_687096ad[13]);
  not not_3 (not_3_out, IR_IN_687096ad[15]);
  CPU_STEPPER cpu_stepper_1 (
    .reset(r), .st(STOP), .clk(clk), .clks(clks), .step_6_40d4d5bc(L_3_11582392), .execute(execute),
    .out_9(cpu_stepper_1_out_9), .step_2_8c45f034(cpu_stepper_1_step_2_8c45f034),
    .step_3_71bf9378(cpu_stepper_1_step_3_71bf9378), .f_e(f_e));  // open: step_4_8482adae, step_5_9168e5f1, step_7_b995d97f, step_8_8b8c5577, step_9_25733d10, step_10_d1921302, step_11_2c52167f, step_12_1f4f3d86, step_13_cd0165a2, step_14_c27f319a, step_15_f0b56f10, step_1_a10c3af4, step_17_1b97b40f, step_18_37d11f24, out_8
  CPU_uCODE_DECODER cpu_ucode_decoder_1 (
    .L_2_1ea30b77(IR_IN_687096ad[5]), .L_1_b91444db(IR_IN_687096ad[4]), .L_4_4d692181(IR_IN_687096ad[7]),
    .L_3_11582392(IR_IN_687096ad[6]), .op(cpu_ucode_decoder_1_op));
  CPU_uCODE_DECODER cpu_ucode_decoder_2 (
    .L_2_1ea30b77(IR_IN_687096ad[1]), .L_1_b91444db(IR_IN_687096ad[0]), .L_4_4d692181(IR_IN_687096ad[3]),
    .L_3_11582392(IR_IN_687096ad[2]), .op(cpu_ucode_decoder_2_op));
  Multiplexer #(.select(2), .width(16)) multiplexer_1 (
    .in0({16{1'b0}}), .in1(cpu_ucode_decoder_2_op), .in2(cpu_ucode_decoder_1_op), .in3({16{1'b0}}),
    .out(RA_RB_E), .sel({Ae, Be}));
  Multiplexer #(.select(2), .width(16)) multiplexer_2 (
    .in0({16{1'b0}}), .in1(cpu_ucode_decoder_1_op), .in2(cpu_ucode_decoder_2_op), .in3({16{1'b0}}),
    .out(RA_RB_S), .sel({Bs, As}));
  or or_10 (or_10_out, cpu_stepper_1_out_9, cpu_ucode_rom_1_out_23, RA_RB_S[15]);
  or or_11 (or_11_out, cpu_stepper_1_out_9, cpu_ucode_rom_1_out_24, RA_RB_S[14]);
  or or_12 (or_12_out, cpu_stepper_1_step_2_8c45f034, cpu_ucode_rom_1_out_25, RA_RB_S[13]);
  or or_13 (or_13_out, cpu_stepper_1_step_3_71bf9378, cpu_ucode_rom_1_out_26, RA_RB_S[12], JI);
  or or_14 (or_14_out, cpu_ucode_rom_1_out_27, RA_RB_S[11]);
  or or_15 (or_15_out, cpu_ucode_rom_1_out_28, RA_RB_S[10]);
  or or_16 (or_16_out, cpu_ucode_rom_1_out_30, RA_RB_S[9]);
  or or_17 (or_17_out, cpu_ucode_rom_1_out_31, RA_RB_S[8]);
  or or_18 (or_18_out, cpu_ucode_rom_1_out_32, RA_RB_S[7]);
  or or_19 (or_19_out, cpu_ucode_rom_1_out_33, RA_RB_S[6]);
  and and_19 (MAR_S, or_10_out, clks);
  and and_20 (ACC_S, or_11_out, clks);
  and and_21 (IR_S, or_12_out, clks);
  and and_22 (IAR_S, or_13_out, clks);
  and and_23 (CNTRL_S, or_14_out, clks);
  and and_24 (TMP_S, or_15_out, clks);
  and and_25 (R6_TMP_S, cpu_ucode_rom_1_out_29, clks);
  and and_26 (FLAGS_S, or_16_out, clks);
  and and_27 (STACK_S, or_17_out, clks);
  and and_28 (INDEX_S, or_18_out, clks);
  and and_29 (FPU_S, or_19_out, clks);
  and and_30 (R5_S, RA_RB_S[5], clks);
  and and_31 (R4_S, RA_RB_S[4], clks);
  and and_32 (R3_S, RA_RB_S[3], clks);
  and and_33 (R2_S, RA_RB_S[2], clks);
  and and_34 (R1_S, RA_RB_S[1], clks);
  and and_35 (R0_S, RA_RB_S[0], clks);
  // also tied to GND on the sheet: {RA_RB_E[10], RA_RB_E[15]}

  // Notes on the sheet:
  //   JUMPIF
  //   INSTRUCTION
endmodule

module CPU_CLK (
  input  clkin,
  output clk,
  output clks,
  output clke
);

  wire j_k_ff_1_qn, nand_1_out;

  J_K_Flip_Flop j_k_ff_1 (.J(1'b1), .clk(clkin), .K(1'b1), .Q(clk), .Qn(j_k_ff_1_qn));  // open: preset, reset
  nand nand_1 (nand_1_out, clkin, clk);
  nand nand_2 (clke, j_k_ff_1_qn, clkin);
  not not_1 (clks, nand_1_out);
endmodule

module CPU_DECODER_2x4 (
  input  a,
  input  b,
  output L_0_5c1f849d,
  output L_1_b91444db,
  output L_2_1ea30b77,
  output L_3_11582392
);

  wire not_1_out, not_2_out;

  not not_1 (not_1_out, b);
  not not_2 (not_2_out, a);
  and and_1 (L_0_5c1f849d, not_2_out, not_1_out);
  and and_2 (L_1_b91444db, a, not_1_out);
  and and_3 (L_2_1ea30b77, b, not_2_out);
  and and_4 (L_3_11582392, b, a);
endmodule

module CPU_DECODER_2x4_WEST (
  input  a,
  input  b,
  output L_0_5c1f849d,
  output L_1_b91444db,
  output L_2_1ea30b77,
  output L_3_11582392
);

  wire not_1_out, not_2_out;

  not not_1 (not_1_out, b);
  not not_2 (not_2_out, a);
  and and_1 (L_0_5c1f849d, not_2_out, not_1_out);
  and and_2 (L_1_b91444db, a, not_1_out);
  and and_3 (L_2_1ea30b77, b, not_2_out);
  and and_4 (L_3_11582392, b, a);
endmodule

module CPU_DECODER_CNTRL_3x8 (
  input  a,
  input  b,
  input  c,
  output L_0_5c1f849d,
  output L_1_b91444db,
  output L_2_1ea30b77,
  output L_3_11582392,
  output L_4_4d692181,
  output L_5_abe02a5b,
  output L_6_f477f93a,
  output L_7_259d2eda
);

  wire not_1_out, not_2_out, not_3_out;

  not not_1 (not_1_out, c);
  not not_2 (not_2_out, b);
  not not_3 (not_3_out, a);
  and and_1 (L_0_5c1f849d, not_3_out, not_2_out, not_1_out);
  and and_2 (L_1_b91444db, not_3_out, not_2_out, c);
  and and_3 (L_2_1ea30b77, not_3_out, b, not_1_out);
  and and_4 (L_3_11582392, not_3_out, b, c);
  and and_5 (L_4_4d692181, a, not_2_out, not_1_out);
  and and_6 (L_5_abe02a5b, a, not_2_out, c);
  and and_7 (L_6_f477f93a, a, b, not_1_out);
  and and_8 (L_7_259d2eda, a, b, c);
endmodule

module CPU_MOTHERBOARD (
  input  CLK_IN,
  input  r,
  input  [7:0] IN1,
  input  [15:0] IN2,
  input  [15:0] IN3,
  input  W,
  output CLKL,
  output CLKE,
  output CLKS,
  output [15:0] R0,
  output [15:0] R1,
  output [15:0] R2,
  output [15:0] R3,
  output END,
  output [15:0] IR,
  output [15:0] IAR,
  output [4:0] FLAGS,
  output [15:0] SP,
  output [7:0] OUT1,
  output [15:0] INDEX,
  output [15:0] FPU,
  output [15:0] OUT2,
  output [15:0] R4,
  output [15:0] out_24,
  output [15:0] R5,
  output [7:0] out_26,
  output [15:0] R6_TEMP,
  output [7:0] OUT3,
  output KYB_CLK,
  output DIS_CLK
);

  wire and_1_out, and_2_out, cpu_address_decoder_1_ram, cpu_address_decoder_1_rom, EN, mc;
  wire [1:0] cpu_1_cntrl_bus;
  wire [3:0] cpu_1_addr_bus;
  wire [7:0] undriven;
  wire [11:0] cpu_1_addr_bus_2;
  wire [15:0] cpu_1_data_bus_out, cpu_input_device_1_bus_out, ram_1_dout, rom_1_data;
  wire [15:8] OUT1_t;

  CPU cpu_1 (
    .clock(CLK_IN), .DATA_BUS_IN(cpu_input_device_1_bus_out), .W(W), .r(r), .out_21(IR), .R6_TMP(R6_TEMP),
    .SP(SP), .INDEX(INDEX), .ADDR_BUS({cpu_1_addr_bus_2, cpu_1_addr_bus}), .CNTRL_BUS(cpu_1_cntrl_bus),
    .END(END), .FU(FPU), .mc(mc), .R0(R0), .clkl(CLKL), .R1(R1), .clke(CLKE), .FLAGS(FLAGS), .clks(CLKS),
    .R2(R2), .R3(R3), .DATA_BUS_OUT(cpu_1_data_bus_out), .R4(R4), .out_22(IAR), .R5(R5));
  CPU_ADDRESS_DECODER cpu_address_decoder_1 (
    .addr({cpu_1_addr_bus_2, cpu_1_addr_bus}), .mc(mc), .i_o(EN), .ram(cpu_address_decoder_1_ram),
    .rom(cpu_address_decoder_1_rom));
  ROM #(.addrWidth(15), .dataWidth(16)) rom_1 (.addr({cpu_1_addr_bus_2[10:0], cpu_1_addr_bus}), .data(rom_1_data));
  CPU_INPUT_DEVICE cpu_input_device_1 (
    .clk_e(cpu_1_cntrl_bus[0]), .en(EN), .id(4'b0000), .in_addr(cpu_1_addr_bus), .r(r),
    .data_in({undriven, IN1}), .bus_out(cpu_input_device_1_bus_out), .io_e(KYB_CLK));  // open: reg_out
  CPU_OUTPUT_DEVICE cpu_output_device_1 (
    .cntrl_s(cpu_1_cntrl_bus[1]), .en(EN), .id(4'b0011), .in_addr(cpu_1_addr_bus),
    .data_in(cpu_1_data_bus_out), .r(r), .data_out({OUT1_t, OUT1}), .io_s(DIS_CLK));  // open: reg_out
  assign cpu_input_device_1_bus_out = and_1_out ? rom_1_data : 16'bz;  // Controlled_Buffer controlled_buffer_1
  and and_1 (and_1_out, cpu_address_decoder_1_rom, cpu_1_cntrl_bus[0]);
  RAM #(.addrWidth(15), .dataWidth(16), .enables("line")) ram_1 (
    .addr({cpu_1_addr_bus_2[10:0], cpu_1_addr_bus}), .we(cpu_address_decoder_1_ram),
    .clk(cpu_1_cntrl_bus[1]), .din(cpu_1_data_bus_out), .dout(ram_1_dout));
  CPU_INPUT_DEVICE cpu_input_device_2 (
    .clk_e(cpu_1_cntrl_bus[0]), .en(EN), .id(4'b0001), .in_addr(cpu_1_addr_bus), .r(r), .data_in(IN2),
    .bus_out(cpu_input_device_1_bus_out));  // open: reg_out, io_e
  CPU_GRAPHICS_1 cpu_graphics_1_1 (
    .id(4'b0100), .in_addr(cpu_1_addr_bus), .mc(mc), .r(r), .data_in(cpu_1_data_bus_out),
    .clk_s(cpu_1_cntrl_bus[1]), .en(EN), .x_y({cpu_1_addr_bus_2, cpu_1_addr_bus}), .X1(out_26), .Y1(OUT3),
    .rgb1(OUT2));  // open: reg_out
  CPU_GRAPHICS_2 cpu_graphics_2_1 (
    .mc(mc), .id(4'b0101), .in_addr(cpu_1_addr_bus), .address({cpu_1_addr_bus_2, cpu_1_addr_bus}),
    .data_in(cpu_1_data_bus_out), .r(r), .clk_s(cpu_1_cntrl_bus[1]), .en(EN), .Y(OUT3), .X(out_26), .rgb(OUT2));  // open: reg_out
  assign cpu_input_device_1_bus_out = and_2_out ? ram_1_dout : 16'bz;  // Controlled_Buffer controlled_buffer_2
  and and_2 (and_2_out, cpu_address_decoder_1_ram, cpu_1_cntrl_bus[0]);
  // CPU_INPUT_DEVICE cpu_input_device_3: pin names not known; wires that end beside it: r, 4'b0010, cpu_1_addr_bus, EN, cpu_1_cntrl_bus[0], IN3, cpu_input_device_1_bus_out

  // Other names for the same wires on the sheet: OUT1_t[7:0] = OUT1; OUT3_t[15:0] = out_24; X1[7:0] = out_26;
  //   Y1[7:0] = OUT3

  // Notes on the sheet:
  //   keyboard
  //   display
  //   contents of rom_1 (hex, n*v repeats v):
  //   108 fff0 c00 8000 332*0 400 fff0 905 4407 4801 5400 4011 0 4c40 15c c00 150 6800 0 0 0 550 800 fff3
  //   4407 4801 5400 4011 0 4c40 16c c00 160 6800
  //   spare
  //   graphics 1
  //   spare
  //   graphics 2
endmodule

module CPU_CARRY_TEMP (
  input  c,
  input  r,
  input  s,
  output o
);

  CPU_MEM_1 cpu_mem_1_1 (.in_1(c), .in_2(s), .r(r), .out_4(o));
endmodule

module LOAD_256_COUNT (
  input  clk,
  input  LOAD,
  input  reset,
  output [7:0] count,
  output carry
);

  wire and_1_out;
  wire [7:0] undriven;

  Counter #(.trigger("falling")) counter_1 (
    .D(undriven), .count(1'b1), .Q(count), .carry(carry), .clk(and_1_out), .clr(reset));  // open: load, up
  and and_1 (and_1_out, LOAD, clk);
endmodule

module CPU_DELAY (
  input  [7:0] i,
  input  clk,
  output [7:0] o
);

  wire undriven;

  Counter #(.ongoal("stay"), .trigger("falling")) counter_1 (
    .load(1'b1), .D(i), .count(undriven), .Q(o), .clk(clk));  // open: carry, up, clr
endmodule

module CPU_TOP_TEMP (
  input  clock
);

  wire and_1_out, C, cpu_accumulator_1_p1, cpu_accumulator_1_p3, cpu_accumulator_1_p4, cpu_alu_1_p4,
       cpu_alu_1_p5, cpu_alu_1_p6, cpu_alu_1_p8, cpu_alu_1_p9, cpu_alu_1_p10, cpu_alu_1_p11,
       cpu_carry_temp_1_o, cpu_clk_1_clk, cpu_clk_1_clke, cpu_clk_1_clks, cpu_control_section_5ba48747_1_p11,
       cpu_control_section_5ba48747_1_p12, cpu_control_section_5ba48747_1_p17,
       cpu_control_section_5ba48747_1_p18, cpu_control_section_5ba48747_1_p19,
       cpu_control_section_5ba48747_1_p20, cpu_control_section_5ba48747_1_p21,
       cpu_control_section_5ba48747_1_p22, cpu_control_section_5ba48747_1_p23,
       cpu_control_section_5ba48747_1_p24, cpu_control_section_5ba48747_1_p25,
       cpu_control_section_5ba48747_1_p26, cpu_control_section_5ba48747_1_p27,
       cpu_control_section_5ba48747_1_p28, cpu_control_section_5ba48747_1_p29,
       cpu_control_section_5ba48747_1_p30, cpu_control_section_5ba48747_1_p31, cpu_flags_1_out_8,
       cpu_flags_1_out_9, cpu_flags_1_out_10, cpu_flags_1_out_11, TMP;
  wire [7:0] cpu_ram_256_1_l_56_ef77dc34, cpu_tmp_1_p1;
  wire [15:0] cpu_bus_1_1_o, cpu_tmp_1_p2;

  // CPU_TMP cpu_tmp_1: pin names not known; wires that end beside it: cpu_tmp_1_p1, cpu_tmp_1_p2, TMP
  // CPU_ACCUMULATOR cpu_accumulator_1: pin names not known; wires that end beside it: cpu_accumulator_1_p1, cpu_tmp_1_p1, cpu_accumulator_1_p3, cpu_accumulator_1_p4
  CPU_BUS_1 cpu_bus_1_1 (.bus_1_0423081d(cpu_control_section_5ba48747_1_p12), .i(cpu_tmp_1_p2), .o(cpu_bus_1_1_o));
  and and_1 (and_1_out, cpu_carry_temp_1_o, C);
  // CPU_ALU cpu_alu_1: pin names not known; wires that end beside it: cpu_tmp_1_p1, cpu_accumulator_1_p1, cpu_bus_1_1_o, cpu_alu_1_p4, cpu_alu_1_p5, cpu_alu_1_p6, and_1_out, cpu_alu_1_p8, cpu_alu_1_p9, cpu_alu_1_p10, cpu_alu_1_p11
  CPU_CLK cpu_clk_1 (.clkin(clock), .clk(cpu_clk_1_clk), .clks(cpu_clk_1_clks), .clke(cpu_clk_1_clke));
  CPU_CARRY_TEMP cpu_carry_temp_1 (.c(cpu_flags_1_out_8), .s(TMP), .o(cpu_carry_temp_1_o));  // open: r
  CPU_FLAGS cpu_flags_1 (
    .C(cpu_alu_1_p8), .A(cpu_alu_1_p9), .E(cpu_alu_1_p10), .Z(cpu_alu_1_p11),
    .s(cpu_control_section_5ba48747_1_p11), .out_8(cpu_flags_1_out_8), .out_9(cpu_flags_1_out_9),
    .out_10(cpu_flags_1_out_10), .out_11(cpu_flags_1_out_11));  // open: r, in_7, op
  // CPU_CONTROL_SECTION_5ba48747 cpu_control_section_5ba48747_1: pin names not known; wires that end beside it: cpu_alu_1_p4, cpu_alu_1_p5, cpu_alu_1_p6, cpu_clk_1_clk, cpu_clk_1_clke, cpu_clk_1_clks, cpu_flags_1_out_8, cpu_flags_1_out_9, cpu_flags_1_out_10, cpu_flags_1_out_11, cpu_control_section_5ba48747_1_p11, cpu_control_section_5ba48747_1_p12, TMP, cpu_accumulator_1_p3, C, cpu_accumulator_1_p4, cpu_control_section_5ba48747_1_p17, cpu_control_section_5ba48747_1_p18, cpu_control_section_5ba48747_1_p19, cpu_control_section_5ba48747_1_p20, cpu_control_section_5ba48747_1_p21, cpu_control_section_5ba48747_1_p22, cpu_control_section_5ba48747_1_p23, cpu_control_section_5ba48747_1_p24, cpu_control_section_5ba48747_1_p25, cpu_control_section_5ba48747_1_p26, cpu_control_section_5ba48747_1_p27, cpu_control_section_5ba48747_1_p28, cpu_control_section_5ba48747_1_p29, cpu_control_section_5ba48747_1_p30, cpu_control_section_5ba48747_1_p31
  // CPU_R cpu_r_1: pin names not known; wires that end beside it: cpu_tmp_1_p1, cpu_control_section_5ba48747_1_p17, cpu_tmp_1_p1, cpu_control_section_5ba48747_1_p18
  // CPU_R cpu_r_2: pin names not known; wires that end beside it: cpu_tmp_1_p1, cpu_control_section_5ba48747_1_p21, cpu_tmp_1_p1, cpu_control_section_5ba48747_1_p22
  // CPU_IAR cpu_iar_1: pin names not known; wires that end beside it: cpu_control_section_5ba48747_1_p19, cpu_tmp_1_p1, cpu_control_section_5ba48747_1_p20, cpu_tmp_1_p1
  // CPU_R cpu_r_3: pin names not known; wires that end beside it: cpu_tmp_1_p1, cpu_control_section_5ba48747_1_p24, cpu_tmp_1_p1, cpu_control_section_5ba48747_1_p26
  // CPU_IR cpu_ir_1: pin names not known; wires that end beside it: cpu_control_section_5ba48747_1_p23, cpu_tmp_1_p1, cpu_control_section_5ba48747_1_p25
  // CPU_R cpu_r_4: pin names not known; wires that end beside it: cpu_tmp_1_p1, cpu_control_section_5ba48747_1_p27, cpu_tmp_1_p1, cpu_control_section_5ba48747_1_p28
  CPU_RAM_256 cpu_ram_256_1 (
    .address(cpu_tmp_1_p1), .i(cpu_tmp_1_p1), .s(cpu_control_section_5ba48747_1_p31),
    .e(cpu_control_section_5ba48747_1_p30), .sa(cpu_control_section_5ba48747_1_p29),
    .L_56_ef77dc34(cpu_ram_256_1_l_56_ef77dc34), .L_55_78950a6b(cpu_ram_256_1_l_56_ef77dc34), .o(cpu_tmp_1_p1));  // open: r, L_107_99897b65, L_123_ddf2dc58, L_139_eae45297, L_155_07d9e508, L_171_bf8c4fbb, L_187_1f89ef21, L_203_a8c39f6c, L_219_0adcfc14, L_11_11cac541, L_235_13495a01, L_251_c363829a, L_27_815ff803, L_43_c3b6d07c, L_59_8c086c19, L_75_24619258, L_91_a710f268, L_106_bfb6d62f, L_122_143bcd3a, L_138_05725277, L_154_6ec9f278, L_170_9f554669, L_186_9a405dd5, L_202_242d9594, L_218_6ec02a7a, L_10_c5a8d897, L_234_44b4ec39, L_250_260a1e1e, L_26_3f41498e, L_42_e66f9d03, L_58_0c5141ff, L_74_585ffe22, L_90_e6684e30, L_105_d7d09b45, L_121_3730566e, L_137_6e77535b, L_153_10b77365, L_169_52386ece, L_185_c2db7a30, L_201_1d2474bb, L_217_6fe273b5, L_9_41cebac5, L_233_e746773c, L_249_ef76f4d3, L_25_2ce4f69c, L_41_b74b1bdb, L_57_0f2507a8, L_73_ddbbd28b, L_89_731f133b, L_104_94ff6a6e, L_120_fb957baa, L_136_eabe134b, L_152_49acf9e5, L_168_f24e050e, L_184_17cfedd4, L_200_e602103d, L_216_4bc9e3e5, L_8_d696b581, L_232_59dbde06, L_248_bd8cab2b, L_24_028bd87a, L_40_55c6a7f1, L_72_39c238b0, L_88_d0c7e292, L_103_4d73e307, L_119_7ef0fc3f, L_135_3b78403a, L_151_085305e2, L_167_0356249c, L_183_50847562, L_199_bf24e250, L_215_5860435c, L_7_259d2eda, L_231_a36fef75, L_247_cde78628, L_23_94ca31e3, L_39_10ebac1e, L_71_5b500dee, L_87_57dc3f4b, L_102_a9d73f14, L_118_67beb245, L_134_42fe3663, L_150_2849742c, L_166_7fb580b8, L_182_ab4227ad, L_198_2c87bdd1, L_214_a6330ace, L_6_f477f93a, L_230_eac81f8e, L_246_3c0a0c8d, L_22_e3a6b9ce, L_38_5524d693, L_54_578b39e6, L_70_c09cf2ba, L_86_d8beac51, L_101_848d6d95, L_117_fda830c3, L_133_fccf8925, L_149_6af5f21c, L_165_d4e84403, L_181_001a9247, L_197_956b7378, L_213_c5f10245, L_5_abe02a5b, L_229_87c6c7fa, L_245_7d3cc3ed, L_21_02550864, L_37_22a518f3, L_53_a28675a9, L_69_92ff2a4c, L_85_549e2dd5, L_100_a50e79c4, L_116_48d4ffce, L_132_60bddf1f, L_148_cc694576, L_164_588b9d2d, L_180_902375d6, L_196_f75650f4, L_212_6087147a, L_4_4d692181, L_228_3a2cdbe1, L_244_071ec77e, L_20_f8652bf4, L_36_24a88140, L_52_3bc4f444, L_68_6960ef71, L_84_3272caa9, L_99_1605b5fb, L_115_9ff82399, L_131_4c1700d0, L_147_dbbc7c10, L_163_71990fdb, L_179_fe58efa3, L_195_a976e483, L_211_5d26a315, out_20, L_227_bed4bf61, L_243_8d097e4a, L_19_575d6bd7, L_35_34e425c9, L_51_eb6257e4, L_67_1f7a3999, L_83_03a2b264, L_98_6862fba1, L_114_c8508d86, L_130_2cb406c6, L_146_984ad7ab, L_162_495b1a62, L_178_ff060783, L_194_b0343b4e, L_210_93d8ec3c, L_2_1ea30b77, L_226_88847811, L_242_4675a6d4, L_18_7afa59f3, L_34_fc51ff66, L_50_d2758f01, L_66_1b20d148, L_82_5190c9a8, L_97_2044529b, L_113_c869e249, L_129_b261d5f4, L_145_2ccf32d2, L_161_d08bfc9e, L_177_ac914753, L_193_9e87d312, L_209_83954787, L_1_b91444db, L_225_b6925578, L_241_ec1bb207, L_17_d1dc3eac, L_33_0e9a6c8e, L_49_946bf74f, L_65_6efbe4b3, L_81_1a1a38e7, L_96_ab7d6c76, L_112_66133eac, L_128_98843eb3, L_144_f0390f9a, L_160_58ec8ce7, L_176_a0b11023, L_192_562a1697, L_208_cdb768a8, L_0_5c1f849d, L_224_2cf65921, L_240_5e7f239c, L_16_55794754, L_32_3d63d3e9, L_48_82b32e2a, L_64_ecf914bb, L_80_2f0332ca, L_111_fae876db, L_127_36bc8e9a, L_143_d47b5445, L_159_a86c72b5, L_175_73e96560, L_191_bd3a36f5, L_207_2339098b, L_223_7315f69d, L_15_ad706d78, L_239_ded08ce8, L_255_a242b549, L_31_156a63a1, L_47_6fe5d602, L_63_b8ad389e, L_79_8403bfd3, L_95_6512fe2e, L_110_67c157ec, L_126_47cccd37, L_142_dff9f878, L_158_147a73cc, L_174_5b8ac4de, L_190_b7e6c28b, L_206_b4c03dfe, L_222_6be29a99, L_14_1024af5c, L_238_f693b788, L_254_f83ca4ac, L_30_c69d1e56, L_46_9037878a, L_62_b3a2e3fd, L_78_b94b47f7, L_94_fbda1007, L_109_e6bc2896, L_125_4d9638ec, L_141_5ad63d84, L_157_ad2d5125, L_173_97570bde, L_189_a1b47a77, L_205_8faab5d2, L_221_0c4aa36a, L_13_95069b4f, L_237_60e138df, L_253_37d8268e, L_29_3ddb3c02, L_45_15c95849, L_61_d2a3d6cd, L_77_25f4e05f, L_93_76d13e06, L_108_06754787, L_124_7f15f756, L_140_e1a95fd0, L_156_d45b8887, L_172_8624c500, L_188_2504910e, L_204_a7861f87, L_220_b073b480, L_12_977d224a, L_236_b35427d6, L_252_9d8fae95, L_28_ccb5c83a, L_44_755bc55f, L_60_44546aba, L_76_88476748, L_92_3c23ad19
endmodule

module temp (
  input  i1,
  input  i2,
  input  i3,
  output i0
);

  wire not_1_out, not_2_out, not_3_out;

  not not_1 (not_1_out, i1);
  not not_2 (not_2_out, i2);
  not not_3 (not_3_out, i3);
  and and_1 (i0, not_1_out, not_2_out, not_3_out);
endmodule

module CPU_INPUT_DEVICE (
  input  [15:0] data_in,
  input  r,
  input  clk_e,
  input  en,
  input  [3:0] id,
  input  [3:0] in_addr,
  output [15:0] reg_out,
  output [15:0] bus_out,
  output io_e
);

  wire and_1_out;
  wire [3:0] xnor_1_out;

  assign xnor_1_out = ~(id ^ in_addr);  // XNOR_Gate xnor_1, 4 bits wide
  and and_1 (and_1_out, xnor_1_out[0], xnor_1_out[1], xnor_1_out[2], xnor_1_out[3]);
  and and_2 (io_e, clk_e, en, and_1_out);
  CPU_REGISTER_16 cpu_register_16_1 (.i(data_in), .r(r), .s(1'b1), .e(io_e), .REG(reg_out), .L_0_5c1f849d(bus_out));
endmodule

module CPU_OUTPUT_DEVICE (
  input  [15:0] data_in,
  input  r,
  input  cntrl_s,
  input  en,
  input  [3:0] id,
  input  [3:0] in_addr,
  output [15:0] reg_out,
  output [15:0] data_out,
  output io_s
);

  wire and_1_out;
  wire [3:0] xnor_1_out;

  assign xnor_1_out = ~(id ^ in_addr);  // XNOR_Gate xnor_1, 4 bits wide
  and and_1 (and_1_out, xnor_1_out[0], xnor_1_out[1], xnor_1_out[2], xnor_1_out[3]);
  and and_2 (io_s, cntrl_s, en, and_1_out);
  CPU_REGISTER_16 cpu_register_16_1 (.i(data_in), .r(r), .s(io_s), .e(1'b1), .REG(reg_out), .L_0_5c1f849d(data_out));
endmodule

module CPU_STEP_MEM (
  input  in_1,
  input  in_2,
  output out_3
);

  wire nand_1_out, nand_2_out, nand_4_out;

  nand nand_1 (nand_1_out, in_1, in_2);
  nand nand_2 (nand_2_out, nand_1_out, in_2);
  nand nand_3 (out_3, nand_1_out, nand_4_out);
  nand nand_4 (nand_4_out, out_3, nand_2_out);
endmodule

module CPU_ADDRESS_DECODER (
  input  [15:0] addr,
  input  mc,
  output i_o,
  output ram,
  output rom
);

  wire and_1_out, and_2_out, not_1_out, not_2_out, not_3_out;

  and and_1 (and_1_out, addr[4], addr[5], addr[6], addr[7], addr[8], addr[9], addr[10], addr[11], addr[12], addr[13], addr[14], addr[15]);
  not not_1 (not_1_out, and_1_out);
  not not_2 (not_2_out, addr[15]);
  and and_2 (and_2_out, not_1_out, addr[15]);
  not not_3 (not_3_out, mc);
  and and_3 (i_o, and_1_out, not_3_out);
  and and_4 (ram, and_2_out, not_3_out);
  and and_5 (rom, not_2_out, not_3_out);
endmodule

module CPU_2x4_CONT (
  input  a,
  input  b,
  output [3:0] op
);

  wire not_1_out, not_2_out;

  not not_1 (not_1_out, b);
  not not_2 (not_2_out, a);
  and and_1 (op[0], not_2_out, not_1_out);
  and and_2 (op[1], a, not_1_out);
  and and_3 (op[2], b, not_2_out);
  and and_4 (op[3], b, a);
endmodule
module CPU_uCode_ROM (
  input  am0,
  input  am1,
  input  [5:0] opcode,
  input  f_e,
  input  [7:0] execute,
  output op,
  output out_7,
  output out_8,
  output out_9,
  output out_10,
  output out_11,
  output out_12,
  output out_13,
  output out_14,
  output out_15,
  output out_16,
  output out_17,
  output out_18,
  output out_19,
  output out_20,
  output out_21,
  output out_22,
  output out_23,
  output out_24,
  output out_25,
  output out_26,
  output out_27,
  output out_28,
  output out_29,
  output out_30,
  output out_31,
  output out_32,
  output out_33,
  output out_34,
  output out_35,
  output out_36,
  output out_37
);

  wire [7:0] adder_1_out;
  wire [9:0] adder_2_out, rom_1_data;
  wire [31:0] rom_2_data;

  ROM #(.dataWidth(10)) rom_1 (.addr(adder_1_out), .data(rom_1_data));
  Adder adder_1 (.a({opcode, am1, am0}), .b({8{1'b0}}), .out(adder_1_out));  // open: cin, cout
  ROM #(.addrWidth(10), .dataWidth(32)) rom_2 (.addr(adder_2_out), .data(rom_2_data));
  Adder #(.width(10)) adder_2 (.a(rom_1_data), .b({2'b00, execute}), .out(adder_2_out), .cin(1'b0));  // open: cout
  Multiplexer #(.width(32)) multiplexer_1 (
    .in0({32{1'b0}}), .in1(rom_2_data),
    .out({op, out_7, out_8, out_9, out_10, out_11, out_12, out_13, out_14, out_15, out_16, out_17, out_18, out_19, out_20, out_21, out_22, out_23, out_24, out_25, out_26, out_27, out_28, out_29, out_30, out_31, out_32, out_33, out_34, out_35, out_36, out_37}),
    .sel(f_e));

  // Notes on the sheet:
  //   contents of rom_1 (hex, n*v repeats v):
  //   0 2 6 10 12 18 1d 22 25 2b 30 35 38 3b 3f 43 45 4d 54 5b 60 68 6c 75 80 88 8c 94 9e a9 ac ae b0 b8
  //   ba bc be c4 c8 d0 da e1 e5 ef fc 103 107 111 11e 125 128 12c 135 13b 13f 147 151 157 15b 163 16d 173
  //   177 17f 189 18e 191 198 1a1 1a4 1a6 1af 1b9 1bc 1c0 1c9 1d3 1d7 1d9 1dc 1e2 1ea 1ec 1ee 1f0 1f2 1f4
  //   1f6 1f8 1fa 1fc 1fe 200 206 20a 212 21c 222 226 22e 238 23e 242 24a 254 258 25a 25c 25e 261
  //   UCode Compress
  //   contents of rom_2 (hex, n*v repeats v):
  //   0 8 906000 1000001 200800 8 804000 1000100 906000 204000 1000020 10004000 2000400 902000 200800 8 0
  //   8 906000 1000100 2004000 1000001 200800 8 80000200 10002000 204000 1000001 8 80004000 1000100
  //   2004000 1000001 8 80004000 1000001 8 906000 1000100 2004000 80000400 200800 8 40000200 10002000
  //   204000 80000400 8 40004000 1000100 2004000 80000400 8 40004000 80000402 8 804000 1000800 8 40000a00
  //   10002000 200001 8 40004000 1000100 2000800 8 40000800 8 8092000 200040 902000 8004000 200400 804000
  //   1000800 8 8092000 204040 800400 40000a00 10002000 200001 8 8092000 204040 800400 40004000 1000100
  //   2000800 8 8092000 204040 800400 80000800 8 8092000 200040 906000 1000100 8004000 2000400 200800 8
  //   8092000 204040 80000400 8 8092000 200040 80004000 1000100 2004000 1000100 8004000 2000400 8 8092000
  //   200040 80004000 1000100 2004000 1000100 8004000 2000400 80082000 200002 8 8086000 200040 1000100
  //   906000 1000020 10004000 2000400 8 8086000 1000001 200040 8 8086000 200040 1000100 40004000 1000020
  //   10004000 2000400 8 8086000 200040 1000100 40004000 1000020 10004000 2000400 40082000 200001 8 906000
  //   1000100 2004000 1000100 204000 1000020 10004000 2000400 902000 200800 8 80000100 2000001 8 0 8 0 8
  //   8092000 204040 80000400 40000002 8086000 1000001 200040 8 0 8 0 8 0 8 906000 200800 1000200 8000a080
  //   200001 8 80000200 4000a080 200001 8 906000 200800 1000100 2004000 1000200 8000a080 200001 8 80004000
  //   1000100 2004000 1000200 4000a080 200001 80004000 1102000 200400 8 906000 200800 1000100 80000200
  //   201a080 200001 8 40000200 8001a080 200001 8 906000 200800 1000100 40004000 1000020 10004000 1000200
  //   201a080 200400 8 906000 200800 1000100 40004000 1000020 10004000 1000200 201a080 200400 10102000
  //   40004000 200400 8 906000 200800 1000100 80000200 202a080 200001 8 40000200 8002a080 200001 8 906000
  //   200800 1000100 40004000 1000020 10004000 1000200 202a080 200400 8 906000 200800 1000100 40004000
  //   1000020 10004000 1000200 202a080 200400 10102000 40004000 200400 8 906000 200800 1000100 2004000
  //   103a080 200400 8 8003a080 200001 8 8003a080 40004000 200400 8 8006a080 40004000 1000100 2004000
  //   80000400 40004000 1102000 200400 8 906000 200800 1000200 8004a080 200001 8 80000200 4004a080 200001
  //   8 906000 200800 1000100 2004000 1000200 8004a080 200001 8 80004000 1000100 2004000 1000200 4004a080
  //   200001 80004000 1102000 200400 8 906000 200800 1000200 8005a080 200001 8 80000200 4005a080 200001 8
  //   906000 200800 1000100 2004000 1000200 8005a080 200001 8 80004000 1000100 2004000 1000200 4005a080
  //   200001 80004000 1102000 200400 8 906000 200800 1000200 8006a080 200001 8 80000200 4006a080 200001 8
  //   906000 200800 1000100 2004000 1000200 8006a080 200001 8 80004000 1000100 2004000 1000200 4006a080
  //   200001 80004000 1102000 200400 8 906000 200800 1000200 40078080 8 40000200 8007a080 8 906000 200800
  //   1000100 2004000 1000200 8007a080 8 80004000 1000100 2004000 1000200 4007a080 200001 80004000 1102000
  //   8 4008a080 200001 8 0 8 804000 1000100 2004000 108a080 2004000 200400 902000 200800 8 80004000
  //   1000100 2004000 1000200 4008a080 200001 80004000 1102000 200400 8 4009a080 200001 8 80000200
  //   4009a080 200001 8 804000 1000100 2004000 109a080 2004000 200400 902000 200800 8 80004000 1000100
  //   2004000 1000200 4009a080 200001 80004000 1102000 200400 8 906000 200800 1000000 8 40000800 8
  //   40004800 1000800 8 40004800 1000800 40004000 1102000 200400 8 80004000 1000100 40004000 1000020
  //   2000400 80004000 10000400 8 0 8 0 8 0 8 100080 8 0 8 0 8 0 8 4 8 0 8 0 8 0 8 906000 200800 1000200
  //   800da080 200001 8 80000200 400da080 200001 8 906000 200800 1000100 2004000 1000200 800da080 200001 8
  //   80004000 1000100 2004000 1000200 400da080 200001 80004000 1102000 200400 8 906000 200800 1000200
  //   800aa080 200001 8 80000200 400aa080 200001 8 906000 200800 1000100 2004000 1000200 800aa080 200001 8
  //   80004000 1000100 2004000 1000200 400aa080 200001 80004000 1102000 200400 8 906000 200800 1000200
  //   800ba080 200001 8 80000200 400ba080 200001 8 906000 200800 1000100 2004000 1000200 800ba080 200001 8
  //   80004000 1000100 2004000 1000200 400ba080 200001 80004000 1102000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
  //   uCode ROM
  //   Outputs
endmodule

module CPU_INC_DEC (
  input  [15:0] in,
  input  r,
  input  S,
  input  E,
  input  ID,
  output [15:0] O
);

  wire not_1_out, xor_1_out;
  wire [15:0] adder_1_out, cpu_register_16_1_l_0_5c1f849d, multiplexer_1_out, multiplexer_2_out,
       subtractor_1_out;

  Subtractor #(.width(16)) subtractor_1 (.a(in), .b(16'h1), .out(subtractor_1_out));  // open: bin, bout
  Adder #(.width(16)) adder_1 (.a(in), .b(16'h1), .out(adder_1_out));  // open: cin, cout
  xor xor_1 (xor_1_out, ID, not_1_out);
  Multiplexer #(.width(16)) multiplexer_1 (
    .in0(subtractor_1_out), .in1(adder_1_out), .out(multiplexer_1_out), .sel(not_1_out));
  // Probe on multiplexer_2_out
  Multiplexer #(.width(16)) multiplexer_2 (.in0(in), .in1(multiplexer_1_out), .out(multiplexer_2_out), .sel(xor_1_out));
  not not_1 (not_1_out, ID);
  CPU_REGISTER_16 cpu_register_16_1 (
    .i(multiplexer_2_out), .r(r), .s(S), .e(E), .L_0_5c1f849d(cpu_register_16_1_l_0_5c1f849d));  // open: REG
  assign O = E ? cpu_register_16_1_l_0_5c1f849d : 16'bz;  // Controlled_Buffer controlled_buffer_1
endmodule

module CPU_ALU_DECODER (
  input  [3:0] in_1,
  output L,
  output out_3,
  output out_4,
  output out_5,
  output out_6,
  output out_7,
  output out_8,
  output out_9,
  output out_10,
  output out_11,
  output out_12,
  output out_13,
  output out_14,
  output out_15,
  output out_16,
  output M
);

  wire not_1_out, not_2_out, not_3_out, not_4_out;

  not not_1 (not_1_out, in_1[0]);
  not not_2 (not_2_out, in_1[1]);
  not not_3 (not_3_out, in_1[2]);
  not not_4 (not_4_out, in_1[3]);
  and and_1 (L, not_4_out, not_3_out, not_2_out, not_1_out);
  and and_2 (out_3, not_4_out, not_3_out, not_2_out, in_1[0]);
  and and_3 (out_4, not_4_out, not_3_out, in_1[1], not_1_out);
  and and_4 (out_5, not_4_out, not_3_out, in_1[1], in_1[0]);
  and and_5 (out_6, not_4_out, in_1[2], not_2_out, not_1_out);
  and and_6 (out_7, not_4_out, in_1[2], not_2_out, in_1[0]);
  and and_7 (out_8, not_4_out, in_1[2], in_1[1], not_1_out);
  and and_8 (out_9, not_4_out, in_1[2], in_1[1], in_1[0]);
  and and_9 (out_10, in_1[3], not_3_out, not_2_out, not_1_out);
  and and_10 (out_11, in_1[3], not_3_out, not_2_out, in_1[0]);
  and and_11 (out_12, in_1[3], not_3_out, in_1[1], not_1_out);
  and and_12 (out_13, in_1[3], not_3_out, in_1[1], in_1[0]);
  and and_13 (out_14, in_1[3], in_1[2], not_2_out, not_1_out);
  and and_14 (out_15, in_1[3], in_1[2], not_2_out, in_1[0]);
  and and_15 (out_16, in_1[3], in_1[2], in_1[1], not_1_out);
  and and_16 (M, in_1[3], in_1[2], in_1[1], in_1[0]);
endmodule

module CPU_uCODE_DECODER (
  input  L_4_4d692181,
  input  L_3_11582392,
  input  L_2_1ea30b77,
  input  L_1_b91444db,
  output [15:0] op
);

  wire not_1_out, not_2_out, not_3_out, not_4_out;

  not not_1 (not_1_out, L_1_b91444db);
  not not_2 (not_2_out, L_2_1ea30b77);
  not not_3 (not_3_out, L_3_11582392);
  not not_4 (not_4_out, L_4_4d692181);
  and and_1 (op[0], not_4_out, not_3_out, not_2_out, not_1_out);
  and and_2 (op[1], not_4_out, not_3_out, not_2_out, L_1_b91444db);
  and and_3 (op[2], not_4_out, not_3_out, L_2_1ea30b77, not_1_out);
  and and_4 (op[3], not_4_out, not_3_out, L_2_1ea30b77, L_1_b91444db);
  and and_5 (op[4], not_4_out, L_3_11582392, not_2_out, not_1_out);
  and and_6 (op[5], not_4_out, L_3_11582392, not_2_out, L_1_b91444db);
  and and_7 (op[6], not_4_out, L_3_11582392, L_2_1ea30b77, not_1_out);
  and and_8 (op[7], not_4_out, L_3_11582392, L_2_1ea30b77, L_1_b91444db);
  and and_9 (op[8], L_4_4d692181, not_3_out, not_2_out, not_1_out);
  and and_10 (op[9], L_4_4d692181, not_3_out, not_2_out, L_1_b91444db);
  and and_11 (op[10], L_4_4d692181, not_3_out, L_2_1ea30b77, not_1_out);
  and and_12 (op[11], L_4_4d692181, not_3_out, L_2_1ea30b77, L_1_b91444db);
  and and_13 (op[12], L_4_4d692181, L_3_11582392, not_2_out, not_1_out);
  and and_14 (op[13], L_4_4d692181, L_3_11582392, not_2_out, L_1_b91444db);
  and and_15 (op[14], L_4_4d692181, L_3_11582392, L_2_1ea30b77, not_1_out);
  and and_16 (op[15], L_4_4d692181, L_3_11582392, L_2_1ea30b77, L_1_b91444db);
endmodule

module CPU_SHIFT (
  input  carry_in_d14b9ec6,
  input  [15:0] i,
  input  [15:0] LRcount,
  input  R,
  input  L,
  output [15:0] out_6,
  output [15:0] op,
  output carry
);

  wire not_1_out;
  wire [0:0] or_1_out;
  wire [15:0] multiplexer_1_out, multiplexer_2_out;
  wire [31:0] shifter_1_out, shifter_2_out;

  or or_1 (or_1_out[0], R, not_1_out);
  not not_1 (not_1_out, L);
  Multiplexer #(.select(2), .width(16)) multiplexer_1 (
    .in0({16{1'b0}}), .in1({16{1'b0}}), .in2(16'h8000), .in3(16'h1), .out(multiplexer_1_out),
    .sel({carry_in_d14b9ec6, or_1_out[0]}));
  Shifter #(.shift("rl"), .width(32)) shifter_1 (
    .in({multiplexer_1_out, i}), .\dist (LRcount[4:0]), .out(shifter_1_out));
  Shifter #(.shift("rr"), .width(32)) shifter_2 (
    .in({multiplexer_1_out, i}), .\dist (LRcount[4:0]), .out(shifter_2_out));
  Multiplexer #(.width(32)) multiplexer_2 (
    .in0(shifter_1_out), .in1(shifter_2_out), .out({multiplexer_2_out, op}), .sel(or_1_out[0]));
  or or_2 (carry, multiplexer_2_out[15], multiplexer_2_out[14], multiplexer_2_out[13], multiplexer_2_out[12], multiplexer_2_out[11], multiplexer_2_out[10], multiplexer_2_out[9], multiplexer_2_out[8], multiplexer_2_out[7], multiplexer_2_out[6], multiplexer_2_out[5], multiplexer_2_out[4], multiplexer_2_out[3], multiplexer_2_out[2], multiplexer_2_out[1], multiplexer_2_out[0]);

  assign out_6 = 16'h8000;

  // Notes on the sheet:
  //   Left = 0
endmodule

module CPU_4x16_CONTROL (
  input  L_3_11582392,
  input  C,
  input  L_2_1ea30b77,
  input  A,
  input  L_1_b91444db,
  input  L_0_5c1f849d,
  input  E,
  input  Z,
  output Ch
);

  wire and_1_out, and_2_out, and_3_out, and_4_out, and_5_out, and_6_out, and_7_out, and_8_out, and_9_out,
       and_10_out, and_11_out, and_12_out, and_13_out, and_14_out, and_15_out, and_16_out, and_17_out,
       and_18_out, and_19_out, and_20_out, and_21_out, and_22_out, and_23_out, and_24_out, and_25_out,
       and_26_out, and_27_out, and_28_out, and_29_out, and_30_out, and_31_out, B, NC, NE, not_5_out,
       not_6_out, not_7_out, not_8_out, NZ;

  not not_1 (NC, C);
  not not_2 (B, A);
  not not_3 (NE, E);
  not not_4 (NZ, Z);
  not not_5 (not_5_out, L_0_5c1f849d);
  not not_6 (not_6_out, L_1_b91444db);
  not not_7 (not_7_out, L_2_1ea30b77);
  not not_8 (not_8_out, L_3_11582392);
  and and_1 (and_1_out, not_8_out, not_7_out, not_6_out, not_5_out);
  and and_2 (and_2_out, not_8_out, not_7_out, not_6_out, L_0_5c1f849d);
  and and_3 (and_3_out, not_8_out, not_7_out, L_1_b91444db, not_5_out);
  and and_4 (and_4_out, not_8_out, not_7_out, L_1_b91444db, L_0_5c1f849d);
  and and_5 (and_5_out, not_8_out, L_2_1ea30b77, not_6_out, not_5_out);
  and and_6 (and_6_out, not_8_out, L_2_1ea30b77, not_6_out, L_0_5c1f849d);
  and and_7 (and_7_out, not_8_out, L_2_1ea30b77, L_1_b91444db, not_5_out);
  and and_8 (and_8_out, not_8_out, L_2_1ea30b77, L_1_b91444db, L_0_5c1f849d);
  and and_9 (and_9_out, L_3_11582392, not_7_out, not_6_out, not_5_out);
  and and_10 (and_10_out, L_3_11582392, not_7_out, not_6_out, L_0_5c1f849d);
  and and_11 (and_11_out, L_3_11582392, not_7_out, L_1_b91444db, not_5_out);
  and and_12 (and_12_out, L_3_11582392, not_7_out, L_1_b91444db, L_0_5c1f849d);
  and and_13 (and_13_out, L_3_11582392, L_2_1ea30b77, not_6_out, not_5_out);
  and and_14 (and_14_out, L_3_11582392, L_2_1ea30b77, not_6_out, L_0_5c1f849d);
  and and_15 (and_15_out, L_3_11582392, L_2_1ea30b77, L_1_b91444db, not_5_out);
  and and_16 (and_16_out, L_3_11582392, L_2_1ea30b77, L_1_b91444db, L_0_5c1f849d);
  and and_17 (and_17_out, and_2_out, C);
  and and_18 (and_18_out, and_3_out, A);
  and and_19 (and_19_out, and_4_out, C, A);
  and and_20 (and_20_out, and_5_out, E);
  or or_1 (Ch, and_17_out, and_18_out, and_19_out, and_20_out, and_21_out, and_22_out, and_23_out, and_24_out, and_25_out, and_26_out, and_27_out, and_28_out, and_29_out, and_30_out, and_31_out);
  and and_21 (and_21_out, and_6_out, C, E);
  and and_22 (and_22_out, and_7_out, A, E);
  and and_23 (and_23_out, and_8_out, C, A, E);
  and and_24 (and_24_out, and_9_out, Z);
  and and_25 (and_25_out, and_10_out, A, E);
  and and_26 (and_26_out, and_11_out, E, Z);
  and and_27 (and_27_out, and_12_out, NE);
  and and_28 (and_28_out, and_13_out, E, Z);
  and and_29 (and_29_out, and_14_out, NC);
  and and_30 (and_30_out, and_15_out, NZ);
  and and_31 (and_31_out, and_16_out, NE, B);

  // Notes on the sheet:
  //   N/A
  //   JC
  //   JA
  //   JCA
  //   JE
  //   JCE
  //   JAE
  //   JCAE
  //   JZ
  //   JCZ
  //   JEZ
  //   JNE
  //   JEZ
  //   JNC
  //   JNZ
  //   JB
  //   No further tests required
  //   No further tests required
  //   No further tests required
  //   Also check JNE this ensures not above , not equals so answer must be below 
endmodule

module CPU_GRAPHICS_1 (
  input  [15:0] x_y,
  input  [15:0] data_in,
  input  r,
  input  clk_s,
  input  en,
  input  [3:0] id,
  input  [3:0] in_addr,
  input  mc,
  output [15:0] reg_out,
  output [7:0] X1,
  output [7:0] Y1,
  output [15:0] rgb1
);

  wire and_1_out, and_2_out, and_3_out, and_4_out, clk, comparator_1_eq, counter_1_carry, counter_2_carry,
       not_1_out, not_2_out;
  wire [3:0] xnor_1_out;
  wire [7:0] counter_1_q, counter_2_q;
  wire [15:0] counter_3_q, cpu_register_16_1_l_0_5c1f849d, multiplexer_1_out, ram_1_dout;

  Clock u_CLK (.out(clk));
  assign xnor_1_out = ~(id ^ in_addr);  // XNOR_Gate xnor_1, 4 bits wide
  and and_1 (and_1_out, xnor_1_out[0], xnor_1_out[1], xnor_1_out[2], xnor_1_out[3]);
  and and_2 (and_2_out, clk_s, en, and_1_out);
  CPU_REGISTER_16 cpu_register_16_1 (
    .i(data_in), .r(r), .s(and_2_out), .e(1'b1), .REG(reg_out), .L_0_5c1f849d(cpu_register_16_1_l_0_5c1f849d));
  and and_3 (and_3_out, clk, not_1_out);
  Counter counter_1 (.Q(counter_1_q), .carry(counter_1_carry), .clk(and_3_out), .clr(r));  // open: load, D, count, up
  not not_1 (not_1_out, and_4_out);
  Comparator #(.mode("unsigned")) comparator_1 (.a(counter_1_q), .b({8{1'b0}}), .eq(comparator_1_eq));  // open: gt, lt
  and and_4 (and_4_out, counter_1_carry, counter_2_carry);
  Counter #(.ongoal("stay")) counter_2 (
    .Q(counter_2_q), .carry(counter_2_carry), .clk(comparator_1_eq));  // open: load, D, count, up, clr
  Counter #(.max('hffff), .width(16)) counter_3 (
    .Q(counter_3_q), .clk(and_3_out), .clr(r));  // open: load, D, count, carry, up
  not not_2 (not_2_out, and_2_out);
  Multiplexer #(.width(16)) multiplexer_1 (.in0(x_y), .in1(counter_3_q), .out(multiplexer_1_out), .sel(not_2_out));
  RAM #(.addrWidth(16), .dataWidth(16), .enables("line")) ram_1 (
    .addr(multiplexer_1_out), .we(not_2_out), .din(cpu_register_16_1_l_0_5c1f849d), .dout(ram_1_dout));  // open: clk
  assign X1 = not_2_out ? counter_1_q : 8'bz;  // Controlled_Buffer controlled_buffer_1
  assign Y1 = not_2_out ? counter_2_q : 8'bz;  // Controlled_Buffer controlled_buffer_2
  assign rgb1 = not_2_out ? ram_1_dout : 16'bz;  // Controlled_Buffer controlled_buffer_3
endmodule

module CPU_GRAPHICS_2 (
  input  [15:0] data_in,
  input  r,
  input  clk_s,
  input  en,
  input  [3:0] id,
  input  [3:0] in_addr,
  input  [15:0] address,
  input  mc,
  output [15:0] reg_out,
  output [15:0] rgb,
  output [7:0] Y,
  output [7:0] X
);

  wire and_1_out, and_2_out, clk, r_t;
  wire [3:0] xnor_1_out;
  wire [7:0] bit_extender_1_out, bit_extender_2_out;
  wire [15:0] cpu_register_16_1_l_0_5c1f849d, divider_1_out, divider_1_rem, register_1_q, register_2_q;

  Clock u_CLK (.out(clk));
  Button RESET (.out(r_t));
  assign xnor_1_out = ~(id ^ in_addr);  // XNOR_Gate xnor_1, 4 bits wide
  Register #(.width(16)) register_1 (.D(address), .Q(register_1_q), .clk(clk_s), .clr(r_t));  // open: en
  and and_1 (and_1_out, xnor_1_out[0], xnor_1_out[1], xnor_1_out[2], xnor_1_out[3]);
  and and_2 (and_2_out, clk_s, en, and_1_out);
  Bit_Extender #(.in_width(16), .out_width(8), .\type ("zero")) bit_extender_1 (
    .in(divider_1_out), .out(bit_extender_1_out));
  Divider #(.width(16)) divider_1 (
    .a(register_1_q), .b(16'h100), .out(divider_1_out), .rem(divider_1_rem));  // open: upper
  Bit_Extender #(.in_width(16), .out_width(8), .\type ("zero")) bit_extender_2 (
    .in(divider_1_rem), .out(bit_extender_2_out));
  CPU_REGISTER_16 cpu_register_16_1 (
    .i(data_in), .r(r), .s(and_2_out), .e(1'b1), .REG(reg_out), .L_0_5c1f849d(cpu_register_16_1_l_0_5c1f849d));
  Register #(.width(16)) register_2 (
    .D(cpu_register_16_1_l_0_5c1f849d), .Q(register_2_q), .clk(clk_s), .clr(r_t));  // open: en
  assign rgb = and_2_out ? register_2_q : 16'bz;  // Controlled_Buffer controlled_buffer_1
  assign Y = and_2_out ? bit_extender_1_out : 8'bz;  // Controlled_Buffer controlled_buffer_2
  assign X = and_2_out ? bit_extender_2_out : 8'bz;  // Controlled_Buffer controlled_buffer_3

  // Other names for the same wires on the sheet: s = clk_s
endmodule
